// Logisim project 实验1-CS1804-U201814604-黄俊淇.circ as structural Verilog: 5 circuits, main circuit 一位二进制半加器
module \一位二进制半加器  (
  input  A,
  input  B,
  output S,
  output C
);

  wire nand_1_out, nand_2_out, nand_3_out;

  nand nand_1 (nand_1_out, A, B);
  nand nand_2 (nand_2_out, A, nand_1_out);
  nand nand_3 (nand_3_out, nand_1_out, B);
  not not_1 (C, nand_1_out);
  nand nand_4 (S, nand_2_out, nand_3_out);
endmodule

module \一位二进制全加器  (
  input  A,
  input  B,
  input  Ci,
  output S,
  output Co
);

  wire nand_1_out, nand_2_out, xor_1_out;

  xor xor_1 (xor_1_out, A, B);
  nand nand_1 (nand_1_out, xor_1_out, Ci);
  nand nand_2 (nand_2_out, B, A);
  xor xor_2 (S, xor_1_out, Ci);
  nand nand_3 (Co, nand_1_out, nand_2_out);
endmodule

module \串行进位并行加法器  (
  input  C0,
  input  A3,
  input  B3,
  input  A1,
  input  B1,
  input  A0,
  input  B0,
  input  A2,
  input  B2,
  output S3,
  output S2,
  output S1,
  output S0,
  output C
);

  wire \一位二进制全加器_2_co , \一位二进制全加器_3_co , \一位二进制全加器_4_co ;

  \一位二进制全加器  \u_一位二进制全加器_1  (.A(A3), .B(B3), .Ci(\一位二进制全加器_2_co ), .S(S3), .Co(C));
  \一位二进制全加器  \u_一位二进制全加器_2  (.A(A2), .B(B2), .Ci(\一位二进制全加器_3_co ), .S(S2), .Co(\一位二进制全加器_2_co ));
  \一位二进制全加器  \u_一位二进制全加器_3  (.A(A1), .B(B1), .Ci(\一位二进制全加器_4_co ), .S(S1), .Co(\一位二进制全加器_3_co ));
  \一位二进制全加器  \u_一位二进制全加器_4  (.A(A0), .B(B0), .Ci(C0), .S(S0), .Co(\一位二进制全加器_4_co ));
endmodule

module \先行进位并行加法器  (
  input  C0,
  input  A1,
  input  B1,
  input  A2,
  input  B2,
  input  A3,
  input  B3,
  input  A4,
  input  B4,
  output S1,
  output S2,
  output S3,
  output S4,
  output C4
);

  wire _21_out, _32_out, _43_out, _210_out, _321_out, _432_out, _3210_out, _4321_out, _43210_out, C1_out,
       C2_out, C3_out, G1_out, G2_out, G3_out, G4_out, P1_out, P1CO_out, P2_out, P3_out, P4_out;

  xor P1 (P1_out, A1, B1);
  and G1 (G1_out, B1, A1);
  xor P2 (P2_out, A2, B2);
  and G2 (G2_out, B2, A2);
  xor P3 (P3_out, A3, B3);
  and G3 (G3_out, B3, A3);
  xor P4 (P4_out, A4, B4);
  and G4 (G4_out, B4, A4);
  and P1CO (P1CO_out, C0, P1_out);
  and _210 (_210_out, P1CO_out, P2_out);
  and _21 (_21_out, P2_out, G1_out);
  or C1 (C1_out, P1CO_out, G1_out);
  or C2 (C2_out, _210_out, _21_out, G2_out);
  and _3210 (_3210_out, _210_out, P3_out);
  and _321 (_321_out, _21_out, P3_out);
  and _32 (_32_out, P3_out, G2_out);
  xor xor_1 (S1, C0, P1_out);
  xor xor_2 (S2, C1_out, P2_out);
  xor xor_3 (S3, C2_out, P3_out);
  or C3 (C3_out, _3210_out, _321_out, _32_out, G3_out);
  and _43210 (_43210_out, _3210_out, P4_out);
  and _4321 (_4321_out, _321_out, P4_out);
  and _432 (_432_out, _32_out, P4_out);
  and _43 (_43_out, P4_out, G3_out);
  xor xor_4 (S4, C3_out, P4_out);
  or u_C4 (C4, _43210_out, _4321_out, _432_out, _43_out, G4_out);
endmodule

module \先行进位并行加法器测试电路  (
  input  C0,
  input  B3,
  input  B2,
  input  B1,
  input  B0,
  input  A3,
  input  A2,
  input  A1,
  input  A0,
  output S3,
  output S2,
  output S1,
  output S0,
  output C4
);

  \先行进位并行加法器  \u_先行进位并行加法器_1  (
    .C0(C0), .A1(A0), .B1(B0), .A2(A1), .B2(B1), .A3(A2), .B3(B2), .A4(A3), .B4(B3), .S1(S0), .S2(S1),
    .S3(S2), .S4(S3), .C4(C4));
endmodule
