// Logisim project 实验2-CS1804-U201814604-黄俊淇.circ as structural Verilog: 14 circuits, main circuit 一位二进制半加器
module \一位二进制半加器  (
  input  A,
  input  B,
  output S,
  output C
);

  wire nand_1_out, nand_2_out, nand_3_out;

  nand nand_1 (nand_1_out, A, B);
  nand nand_2 (nand_2_out, A, nand_1_out);
  nand nand_3 (nand_3_out, nand_1_out, B);
  not not_1 (C, nand_1_out);
  nand nand_4 (S, nand_2_out, nand_3_out);
endmodule

module \一位二进制全加器  (
  input  A,
  input  B,
  input  Ci,
  output S,
  output Co
);

  wire nand_1_out, nand_2_out, xor_1_out;

  xor xor_1 (xor_1_out, A, B);
  nand nand_1 (nand_1_out, xor_1_out, Ci);
  nand nand_2 (nand_2_out, B, A);
  xor xor_2 (S, xor_1_out, Ci);
  nand nand_3 (Co, nand_1_out, nand_2_out);
endmodule

module \串行进位并行加法器  (
  input  C0,
  input  A3,
  input  B3,
  input  A1,
  input  B1,
  input  A0,
  input  B0,
  input  A2,
  input  B2,
  output S3,
  output S2,
  output S1,
  output S0,
  output C
);

  wire \一位二进制全加器_2_co , \一位二进制全加器_3_co , \一位二进制全加器_4_co ;

  \一位二进制全加器  \u_一位二进制全加器_1  (.A(A3), .B(B3), .Ci(\一位二进制全加器_2_co ), .S(S3), .Co(C));
  \一位二进制全加器  \u_一位二进制全加器_2  (.A(A2), .B(B2), .Ci(\一位二进制全加器_3_co ), .S(S2), .Co(\一位二进制全加器_2_co ));
  \一位二进制全加器  \u_一位二进制全加器_3  (.A(A1), .B(B1), .Ci(\一位二进制全加器_4_co ), .S(S1), .Co(\一位二进制全加器_3_co ));
  \一位二进制全加器  \u_一位二进制全加器_4  (.A(A0), .B(B0), .Ci(C0), .S(S0), .Co(\一位二进制全加器_4_co ));
endmodule

module \先行进位并行加法器  (
  input  C0,
  input  A1,
  input  B1,
  input  A2,
  input  B2,
  input  A3,
  input  B3,
  input  A4,
  input  B4,
  output S1,
  output S2,
  output S3,
  output S4,
  output C4
);

  wire _21_out, _32_out, _43_out, _210_out, _321_out, _432_out, _3210_out, _4321_out, _43210_out, C1_out,
       C2_out, C3_out, G1_out, G2_out, G3_out, G4_out, P1_out, P1CO_out, P2_out, P3_out, P4_out;

  xor P1 (P1_out, A1, B1);
  and G1 (G1_out, B1, A1);
  xor P2 (P2_out, A2, B2);
  and G2 (G2_out, B2, A2);
  xor P3 (P3_out, A3, B3);
  and G3 (G3_out, B3, A3);
  xor P4 (P4_out, A4, B4);
  and G4 (G4_out, B4, A4);
  and P1CO (P1CO_out, C0, P1_out);
  and _210 (_210_out, P1CO_out, P2_out);
  and _21 (_21_out, P2_out, G1_out);
  or C1 (C1_out, P1CO_out, G1_out);
  or C2 (C2_out, _210_out, _21_out, G2_out);
  and _3210 (_3210_out, _210_out, P3_out);
  and _321 (_321_out, _21_out, P3_out);
  and _32 (_32_out, P3_out, G2_out);
  xor xor_1 (S1, C0, P1_out);
  xor xor_2 (S2, C1_out, P2_out);
  xor xor_3 (S3, C2_out, P3_out);
  or C3 (C3_out, _3210_out, _321_out, _32_out, G3_out);
  and _43210 (_43210_out, _3210_out, P4_out);
  and _4321 (_4321_out, _321_out, P4_out);
  and _432 (_432_out, _32_out, P4_out);
  and _43 (_43_out, P4_out, G3_out);
  xor xor_4 (S4, C3_out, P4_out);
  or u_C4 (C4, _43210_out, _4321_out, _432_out, _43_out, G4_out);
endmodule

module \先行进位并行加法器测试电路  (
  input  C0,
  input  B3,
  input  B2,
  input  B1,
  input  B0,
  input  A3,
  input  A2,
  input  A1,
  input  A0,
  output S3,
  output S2,
  output S1,
  output S0,
  output C4
);

  \先行进位并行加法器  \u_先行进位并行加法器_1  (
    .C0(C0), .A1(A0), .B1(B0), .A2(A1), .B2(B1), .A3(A2), .B3(B2), .A4(A3), .B4(B3), .S1(S0), .S2(S1),
    .S3(S2), .S4(S3), .C4(C4));
endmodule

module \四位二进制可逆计数器  (
  input  CPU,
  input  CLR,
  input  LD,
  input  A,
  input  B,
  input  C,
  input  D,
  input  CPD,
  output QA,
  output QB,
  output QC,
  output QD
);

  wire and_1_out, and_2_out, and_3_out, and_4_out, and_5_out, and_6_out, and_7_out, and_8_out, and_9_out,
       and_10_out, and_11_out, and_12_out, and_13_out, and_14_out, c2_out, c3_out, c4_out, not_1_out,
       not_2_out, not_3_out, not_4_out, not_5_out, not_6_out, not_7_out, not_8_out, not_9_out, or_1_out,
       or_2_out, or_3_out, or_4_out, or_5_out;

  or or_1 (or_1_out, CPU, CPD);
  not not_1 (not_1_out, QA);
  not not_2 (not_2_out, QB);
  not not_3 (not_3_out, QC);
  and and_1 (and_1_out, not_1_out, CPD);
  and and_2 (and_2_out, QA, CPU);
  and and_3 (and_3_out, not_1_out, not_2_out, CPD);
  and and_4 (and_4_out, QA, QB, CPU);
  and and_5 (and_5_out, not_1_out, not_2_out, not_3_out, CPD);
  and and_6 (and_6_out, QA, QB, QC, CPU);
  D_Flip_Flop #(.trigger("falling")) d_ff_1 (
    .clk(or_1_out), .D(not_1_out), .Q(QA), .preset(and_7_out), .reset(or_2_out));  // open: Qn, en
  or c2 (c2_out, and_1_out, and_2_out);
  or c3 (c3_out, and_3_out, and_4_out);
  or c4 (c4_out, and_5_out, and_6_out);
  not not_4 (not_4_out, QD);
  and and_7 (and_7_out, A, not_9_out);
  or or_2 (or_2_out, and_13_out, CLR);
  D_Flip_Flop #(.trigger("falling")) d_ff_2 (
    .clk(c2_out), .D(not_2_out), .Q(QB), .preset(and_8_out), .reset(or_3_out));  // open: Qn, en
  and and_8 (and_8_out, not_9_out, B);
  or or_3 (or_3_out, CLR, and_14_out);
  D_Flip_Flop #(.trigger("falling")) d_ff_3 (
    .clk(c3_out), .D(not_3_out), .Q(QC), .preset(and_9_out), .reset(or_4_out));  // open: Qn, en
  and and_9 (and_9_out, not_9_out, C);
  or or_4 (or_4_out, CLR, and_10_out);
  and and_10 (and_10_out, not_9_out, not_7_out);
  D_Flip_Flop #(.trigger("falling")) d_ff_4 (
    .clk(c4_out), .D(not_4_out), .Q(QD), .preset(and_11_out), .reset(or_5_out));  // open: Qn, en
  and and_11 (and_11_out, not_9_out, D);
  and and_12 (and_12_out, not_9_out, not_8_out);
  or or_5 (or_5_out, and_12_out, CLR);
  and and_13 (and_13_out, not_9_out, not_5_out);
  not not_5 (not_5_out, A);
  and and_14 (and_14_out, not_9_out, not_6_out);
  not not_6 (not_6_out, B);
  not not_7 (not_7_out, C);
  not not_8 (not_8_out, D);
  not not_9 (not_9_out, LD);
endmodule

module \四位二进制可逆计数器测试电路  (
  input  CPu,
  input  CLR,
  input  CPd,
  input  D,
  input  C,
  input  B,
  input  A,
  input  LD,
  output QD,
  output QC,
  output QB,
  output QA
);

  \四位二进制可逆计数器  \u_四位二进制可逆计数器_1  (
    .CPU(CPu), .CPD(CPd), .CLR(CLR), .LD(LD), .A(A), .B(B), .C(C), .D(D), .QA(QA), .QB(QB), .QC(QC), .QD(QD));
endmodule

module \二进制转8421码电路  (
  input  A3,
  input  A2,
  input  A1,
  input  A0,
  output S3,
  output S2,
  output S1,
  output S0,
  output C4
);

  wire and_1_out, or_1_out;

  or or_1 (or_1_out, A1, A2);
  and and_1 (and_1_out, A3, or_1_out);
  \先行进位并行加法器  \u_先行进位并行加法器_1  (
    .C0(1'b0), .A1(A0), .B1(1'b0), .A2(A1), .B2(and_1_out), .A3(A2), .B3(and_1_out), .A4(A3), .B4(1'b0),
    .S1(S0), .S2(S1), .S3(S2), .S4(S3), .C4(C4));
endmodule

module \二进制转8421码测试电路  (
  input  A3,
  input  A2,
  input  A1,
  input  A0,
  output S3,
  output S2,
  output S1,
  output S0,
  output c4
);

  \二进制转8421码电路  \u_二进制转8421码电路_1  (.C4(c4), .S3(S3), .S2(S2), .S1(S1), .S0(S0), .A3(A3), .A2(A2), .A1(A1), .A0(A0));
endmodule

module \显示电路  (
  input  A3,
  input  A2,
  input  A1,
  input  A0,
  output a,
  output b,
  output c,
  output d,
  output e,
  output f,
  output g
);

  wire and_1_out, and_2_out, and_3_out, and_4_out, and_5_out, and_6_out, and_7_out, and_8_out, and_9_out,
       and_10_out, and_11_out, and_12_out, and_13_out, and_14_out, and_15_out, and_16_out, and_17_out,
       and_18_out, and_19_out, and_20_out, and_21_out, and_22_out, and_23_out, and_24_out, and_25_out,
       and_26_out, not_1_out, not_2_out, not_3_out, not_4_out, not_5_out, not_6_out, not_7_out, not_8_out,
       not_9_out, not_10_out, not_11_out, not_12_out, not_13_out, not_14_out, not_15_out, not_16_out,
       not_17_out, not_18_out, not_19_out, not_20_out, not_21_out, not_22_out, not_23_out, not_24_out,
       not_25_out, not_26_out, not_27_out, not_28_out, not_29_out, not_30_out, not_31_out, not_32_out,
       not_33_out, not_34_out, not_35_out, not_36_out, not_37_out;

  not not_1 (not_1_out, A3);
  not not_2 (not_2_out, A2);
  not not_3 (not_3_out, A0);
  not not_4 (not_4_out, A3);
  not not_5 (not_5_out, A2);
  not not_6 (not_6_out, A3);
  not not_7 (not_7_out, A2);
  not not_8 (not_8_out, A1);
  not not_9 (not_9_out, A1);
  not not_10 (not_10_out, A3);
  not not_11 (not_11_out, A2);
  not not_12 (not_12_out, A2);
  not not_13 (not_13_out, A1);
  not not_14 (not_14_out, A1);
  not not_15 (not_15_out, A0);
  not not_16 (not_16_out, A3);
  not not_17 (not_17_out, A2);
  not not_18 (not_18_out, A1);
  not not_19 (not_19_out, A2);
  not not_20 (not_20_out, A3);
  not not_21 (not_21_out, A2);
  not not_22 (not_22_out, A0);
  not not_23 (not_23_out, A2);
  not not_24 (not_24_out, A0);
  not not_25 (not_25_out, A1);
  not not_26 (not_26_out, A2);
  not not_27 (not_27_out, A0);
  not not_28 (not_28_out, A0);
  not not_29 (not_29_out, A1);
  not not_30 (not_30_out, A0);
  not not_31 (not_31_out, A1);
  not not_32 (not_32_out, A0);
  not not_33 (not_33_out, A1);
  not not_34 (not_34_out, A2);
  not not_35 (not_35_out, A1);
  not not_36 (not_36_out, A0);
  not not_37 (not_37_out, A2);
  and and_1 (and_1_out, not_1_out, not_2_out, not_3_out);
  and and_2 (and_2_out, not_4_out, not_5_out, A1);
  and and_3 (and_3_out, not_6_out, A2, A0);
  and and_4 (and_4_out, not_7_out, not_8_out, A3);
  and and_5 (and_5_out, A3, not_9_out, A0);
  and and_6 (and_6_out, not_10_out, not_11_out);
  and and_7 (and_7_out, not_12_out, not_13_out);
  and and_8 (and_8_out, not_14_out, not_15_out);
  and and_9 (and_9_out, not_16_out, A1, A0);
  and and_10 (and_10_out, not_17_out, not_18_out);
  and and_11 (and_11_out, not_19_out, A0);
  and and_12 (and_12_out, not_20_out, A2);
  and and_13 (and_13_out, not_21_out, not_22_out);
  and and_14 (and_14_out, not_23_out, A1);
  and and_15 (and_15_out, A1, not_24_out);
  and and_16 (and_16_out, A2, not_25_out, A0);
  and and_17 (and_17_out, not_26_out, not_27_out);
  and and_18 (and_18_out, A1, not_28_out);
  and and_19 (and_19_out, not_29_out, not_30_out);
  and and_20 (and_20_out, A2, not_31_out);
  and and_21 (and_21_out, A2, not_32_out);
  and and_22 (and_22_out, A3, not_33_out);
  and and_23 (and_23_out, not_34_out, A1);
  and and_24 (and_24_out, A2, not_35_out);
  and and_25 (and_25_out, A2, not_36_out);
  and and_26 (and_26_out, A3, not_37_out);
  or or_1 (f, and_19_out, and_20_out, and_21_out, and_22_out);
  or or_2 (a, and_1_out, and_2_out, and_3_out, and_4_out, and_5_out);
  or or_3 (b, and_6_out, and_7_out, and_8_out, and_9_out);
  or or_4 (c, and_10_out, and_11_out, and_12_out);
  or or_5 (d, and_13_out, and_14_out, and_15_out, and_16_out);
  or or_6 (e, and_17_out, and_18_out);
  or or_7 (g, and_23_out, and_24_out, and_25_out, and_26_out);
endmodule

module \显示电路测试电路  (
  input  A3,
  input  A2,
  input  A1,
  input  A0
);

  wire \二进制转8421码电路_1_c4 , \二进制转8421码电路_1_s0 , \二进制转8421码电路_1_s1 , \二进制转8421码电路_1_s2 , \二进制转8421码电路_1_s3 ,
       \显示电路_1_a , \显示电路_1_b , \显示电路_1_c , \显示电路_1_d , \显示电路_1_e , \显示电路_1_f , \显示电路_1_g , \显示电路_2_a ,
       \显示电路_2_b , \显示电路_2_c , \显示电路_2_d , \显示电路_2_e , \显示电路_2_f , \显示电路_2_g ;

  _7_Segment_Display u_7_segment_display_1 (
    .g(\显示电路_1_g ), .f(\显示电路_1_f ), .a(\显示电路_1_a ), .b(\显示电路_1_b ), .e(\显示电路_1_e ), .d(\显示电路_1_d ),
    .c(\显示电路_1_c ), .dp(1'b0));
  \显示电路  \u_显示电路_1  (
    .A3(1'b0), .A2(1'b0), .A1(1'b0), .A0(\二进制转8421码电路_1_c4 ), .a(\显示电路_1_a ), .b(\显示电路_1_b ), .c(\显示电路_1_c ),
    .d(\显示电路_1_d ), .e(\显示电路_1_e ), .f(\显示电路_1_f ), .g(\显示电路_1_g ));
  \显示电路  \u_显示电路_2  (
    .A3(\二进制转8421码电路_1_s3 ), .A2(\二进制转8421码电路_1_s2 ), .A1(\二进制转8421码电路_1_s1 ), .A0(\二进制转8421码电路_1_s0 ),
    .a(\显示电路_2_a ), .b(\显示电路_2_b ), .c(\显示电路_2_c ), .d(\显示电路_2_d ), .e(\显示电路_2_e ), .f(\显示电路_2_f ),
    .g(\显示电路_2_g ));
  _7_Segment_Display u_7_segment_display_2 (
    .g(\显示电路_2_g ), .f(\显示电路_2_f ), .a(\显示电路_2_a ), .b(\显示电路_2_b ), .e(\显示电路_2_e ), .d(\显示电路_2_d ),
    .c(\显示电路_2_c ), .dp(1'b0));
  \二进制转8421码电路  \u_二进制转8421码电路_1  (
    .C4(\二进制转8421码电路_1_c4 ), .S3(\二进制转8421码电路_1_s3 ), .S2(\二进制转8421码电路_1_s2 ), .S1(\二进制转8421码电路_1_s1 ),
    .S0(\二进制转8421码电路_1_s0 ), .A3(A3), .A2(A2), .A1(A1), .A0(A0));
endmodule

module \报警电路  (
  input  CPu,
  input  CLR,
  input  CPd,
  input  D,
  input  C,
  input  B,
  input  A,
  output QD,
  output QC,
  output QB,
  output QA,
  output Z
);

  wire and_2_out, and_3_out, and_4_out, not_1_out, or_1_out;

  and and_1 (Z, and_2_out, CPu);
  or or_1 (or_1_out, QA, QB, QC, QD);
  not not_1 (not_1_out, and_2_out);
  and and_2 (and_2_out, QD, QC, QB, QA);
  and and_3 (and_3_out, not_1_out, CPu);
  and and_4 (and_4_out, or_1_out, CPd);
  \四位二进制可逆计数器  \u_四位二进制可逆计数器_1  (
    .CPU(and_3_out), .CPD(and_4_out), .CLR(CLR), .LD(1'b1), .A(A), .B(B), .C(C), .D(D), .QA(QA), .QB(QB),
    .QC(QC), .QD(QD));
endmodule

module \小型实验室门禁系统  (
  input  CPu,
  input  CLR,
  input  CPd,
  input  D,
  input  C,
  input  B,
  input  A,
  output Q,
  output Q_2,
  output Q_3,
  output Q_4,
  output Q_5,
  output Q_6,
  output Q_7,
  output Q_8,
  output Q_9,
  output Q_10,
  output Q_11,
  output Q_12,
  output Q_13,
  output Q_14,
  output Q_15
);

  wire \二进制转8421码电路_1_c4 , \二进制转8421码电路_1_s0 , \二进制转8421码电路_1_s1 , \二进制转8421码电路_1_s2 , \二进制转8421码电路_1_s3 ,
       \报警电路_1_qa , \报警电路_1_qb , \报警电路_1_qc , \报警电路_1_qd ;

  \显示电路  \u_显示电路_1  (
    .A3(1'b0), .A2(1'b0), .A1(1'b0), .A0(\二进制转8421码电路_1_c4 ), .a(Q), .b(Q_2), .c(Q_3), .d(Q_4), .e(Q_5),
    .f(Q_6), .g(Q_7));
  \显示电路  \u_显示电路_2  (
    .A3(\二进制转8421码电路_1_s3 ), .A2(\二进制转8421码电路_1_s2 ), .A1(\二进制转8421码电路_1_s1 ), .A0(\二进制转8421码电路_1_s0 ),
    .a(Q_8), .b(Q_9), .c(Q_10), .d(Q_11), .e(Q_12), .f(Q_13), .g(Q_14));
  \报警电路  \u_报警电路_1  (
    .CPu(CPu), .CLR(CLR), .CPd(CPd), .Z(Q_15), .QD(\报警电路_1_qd ), .QC(\报警电路_1_qc ), .QB(\报警电路_1_qb ),
    .QA(\报警电路_1_qa ), .D(D), .C(C), .B(B), .A(A));
  \二进制转8421码电路  \u_二进制转8421码电路_1  (
    .C4(\二进制转8421码电路_1_c4 ), .S3(\二进制转8421码电路_1_s3 ), .S2(\二进制转8421码电路_1_s2 ), .S1(\二进制转8421码电路_1_s1 ),
    .S0(\二进制转8421码电路_1_s0 ), .A3(\报警电路_1_qd ), .A2(\报警电路_1_qc ), .A1(\报警电路_1_qb ), .A0(\报警电路_1_qa ));
endmodule

module \小型门禁系统测试电路  (
  input  CPu,
  input  CLR,
  input  CPd,
  input  D,
  input  C,
  input  B,
  input  A
);

  wire \小型实验室门禁系统_1_q , \小型实验室门禁系统_1_q_2 , \小型实验室门禁系统_1_q_3 , \小型实验室门禁系统_1_q_4 , \小型实验室门禁系统_1_q_5 ,
       \小型实验室门禁系统_1_q_6 , \小型实验室门禁系统_1_q_7 , \小型实验室门禁系统_1_q_8 , \小型实验室门禁系统_1_q_9 , \小型实验室门禁系统_1_q_10 ,
       \小型实验室门禁系统_1_q_11 , \小型实验室门禁系统_1_q_12 , \小型实验室门禁系统_1_q_13 , \小型实验室门禁系统_1_q_14 , \小型实验室门禁系统_1_q_15 ;

  _7_Segment_Display u_7_segment_display_1 (
    .g(\小型实验室门禁系统_1_q_7 ), .f(\小型实验室门禁系统_1_q_6 ), .a(\小型实验室门禁系统_1_q ), .b(\小型实验室门禁系统_1_q_2 ),
    .e(\小型实验室门禁系统_1_q_5 ), .d(\小型实验室门禁系统_1_q_4 ), .c(\小型实验室门禁系统_1_q_3 ), .dp(1'b0));
  _7_Segment_Display u_7_segment_display_2 (
    .g(\小型实验室门禁系统_1_q_14 ), .f(\小型实验室门禁系统_1_q_13 ), .a(\小型实验室门禁系统_1_q_8 ), .b(\小型实验室门禁系统_1_q_9 ),
    .e(\小型实验室门禁系统_1_q_12 ), .d(\小型实验室门禁系统_1_q_11 ), .c(\小型实验室门禁系统_1_q_10 ), .dp(1'b0));
  LED led_1 (.in(\小型实验室门禁系统_1_q_15 ));
  \小型实验室门禁系统  \u_小型实验室门禁系统_1  (
    .CPu(CPu), .CLR(CLR), .CPd(CPd), .Q_15(\小型实验室门禁系统_1_q_15 ), .Q(\小型实验室门禁系统_1_q ), .Q_2(\小型实验室门禁系统_1_q_2 ),
    .Q_3(\小型实验室门禁系统_1_q_3 ), .Q_4(\小型实验室门禁系统_1_q_4 ), .Q_5(\小型实验室门禁系统_1_q_5 ), .Q_6(\小型实验室门禁系统_1_q_6 ),
    .Q_7(\小型实验室门禁系统_1_q_7 ), .Q_8(\小型实验室门禁系统_1_q_8 ), .Q_9(\小型实验室门禁系统_1_q_9 ), .Q_10(\小型实验室门禁系统_1_q_10 ),
    .Q_11(\小型实验室门禁系统_1_q_11 ), .Q_12(\小型实验室门禁系统_1_q_12 ), .Q_13(\小型实验室门禁系统_1_q_13 ),
    .Q_14(\小型实验室门禁系统_1_q_14 ), .D(D), .C(C), .B(B), .A(A));
endmodule
