// Logisim project 实验3-CS1804-U201814604-黄俊淇.circ as structural Verilog: 6 circuits, main circuit 四位乘法器
module \四位乘法器  (
  input  [3:0] in_1,
  input  [3:0] in_2,
  output [7:0] out_3
);

  wire [7:0] adder_1_out, adder_2_out, adder_3_out, adder_4_out, bit_extender_1_out, multiplexer_1_out,
       multiplexer_2_out, multiplexer_3_out, shifter_1_out, shifter_2_out, shifter_3_out;

  assign bit_extender_1_out = {{4{1'b0}}, in_2};  // Bit_Extender bit_extender_1
  Adder #(.width(8)) adder_1 (.a({8{1'b0}}), .b(bit_extender_1_out), .out(adder_1_out), .cin(1'b0));  // open: cout
  Shifter #(.width(8), .shift("ll")) shifter_1 (.in(bit_extender_1_out), .\dist (3'b001), .out(shifter_1_out));
  Multiplexer #(.select(1), .width(8), .disabled("Z"), .enable("false")) multiplexer_1 (
    .in0({8{1'b0}}), .in1(adder_1_out), .out(multiplexer_1_out), .sel(in_1[0]));
  Adder #(.width(8)) adder_2 (.a(multiplexer_1_out), .b(shifter_1_out), .out(adder_2_out), .cin(1'b0));  // open: cout
  Shifter #(.width(8), .shift("ll")) shifter_2 (.in(shifter_1_out), .\dist (3'b001), .out(shifter_2_out));
  Multiplexer #(.select(1), .width(8), .disabled("Z"), .enable("false")) multiplexer_2 (
    .in0(multiplexer_1_out), .in1(adder_2_out), .out(multiplexer_2_out), .sel(in_1[1]));
  Adder #(.width(8)) adder_3 (.a(multiplexer_2_out), .b(shifter_2_out), .out(adder_3_out), .cin(1'b0));  // open: cout
  Multiplexer #(.select(1), .width(8), .disabled("Z"), .enable("false")) multiplexer_3 (
    .in0(multiplexer_2_out), .in1(adder_3_out), .out(multiplexer_3_out), .sel(in_1[2]));
  Shifter #(.width(8), .shift("ll")) shifter_3 (.in(shifter_2_out), .\dist (3'b001), .out(shifter_3_out));
  Multiplexer #(.select(1), .width(8), .disabled("Z"), .enable("false")) multiplexer_4 (
    .in0(multiplexer_3_out), .in1(adder_4_out), .out(out_3), .sel(in_1[3]));
  Adder #(.width(8)) adder_4 (.a(multiplexer_3_out), .b(shifter_3_out), .out(adder_4_out), .cin(1'b0));  // open: cout
  Shifter #(.width(8), .shift("ll")) shifter_4 (.in(shifter_3_out), .\dist (3'b001));  // open: out
endmodule

module \四位乘法器测试电路  (
  input  [3:0] in_1,
  input  [3:0] in_2,
  output [7:0] out_3
);

  \四位乘法器  \u_四位乘法器_1  (.in_2(in_2), .out_3(out_3), .in_1(in_1));
endmodule

module \_32X4乘法器  (
  input  [3:0] in_1,
  input  [31:0] in_2,
  output [31:0] out_3,
  output [31:0] out_4
);

  wire adder_6_cout, adder_8_cout;
  wire [7:0] \四位乘法器_1_out_3 , \四位乘法器_2_out_3 , \四位乘法器_3_out_3 , \四位乘法器_4_out_3 , \四位乘法器_5_out_3 ,
       \四位乘法器_6_out_3 , \四位乘法器_7_out_3 , \四位乘法器_8_out_3 ;
  wire [31:0] adder_1_out, adder_2_out, adder_3_out, adder_4_out, adder_5_out, adder_6_out,
       bit_extender_1_out, bit_extender_2_out, bit_extender_3_out, bit_extender_4_out, bit_extender_5_out,
       bit_extender_6_out, bit_extender_7_out, bit_extender_8_out, bit_extender_9_out, bit_extender_10_out,
       shifter_1_out, shifter_2_out, shifter_3_out, shifter_4_out, shifter_5_out, shifter_6_out,
       shifter_7_out;

  \四位乘法器  \u_四位乘法器_1  (.in_2(in_2[3:0]), .out_3(\四位乘法器_1_out_3 ), .in_1(in_1));
  \四位乘法器  \u_四位乘法器_2  (.in_2(in_2[7:4]), .out_3(\四位乘法器_2_out_3 ), .in_1(in_1));
  \四位乘法器  \u_四位乘法器_3  (.in_2(in_2[11:8]), .out_3(\四位乘法器_3_out_3 ), .in_1(in_1));
  \四位乘法器  \u_四位乘法器_4  (.in_2(in_2[15:12]), .out_3(\四位乘法器_4_out_3 ), .in_1(in_1));
  \四位乘法器  \u_四位乘法器_5  (.in_2(in_2[19:16]), .out_3(\四位乘法器_5_out_3 ), .in_1(in_1));
  \四位乘法器  \u_四位乘法器_6  (.in_2(in_2[23:20]), .out_3(\四位乘法器_6_out_3 ), .in_1(in_1));
  \四位乘法器  \u_四位乘法器_7  (.in_2(in_2[27:24]), .out_3(\四位乘法器_7_out_3 ), .in_1(in_1));
  \四位乘法器  \u_四位乘法器_8  (.in_2(in_2[31:28]), .out_3(\四位乘法器_8_out_3 ), .in_1(in_1));
  assign bit_extender_1_out = {{24{1'b0}}, \四位乘法器_1_out_3 };  // Bit_Extender bit_extender_1
  assign bit_extender_2_out = {{24{1'b0}}, \四位乘法器_2_out_3 };  // Bit_Extender bit_extender_2
  assign bit_extender_3_out = {{24{1'b0}}, \四位乘法器_3_out_3 };  // Bit_Extender bit_extender_3
  assign bit_extender_4_out = {{24{1'b0}}, \四位乘法器_4_out_3 };  // Bit_Extender bit_extender_4
  assign bit_extender_5_out = {{24{1'b0}}, \四位乘法器_5_out_3 };  // Bit_Extender bit_extender_5
  assign bit_extender_6_out = {{24{1'b0}}, \四位乘法器_6_out_3 };  // Bit_Extender bit_extender_6
  assign bit_extender_7_out = {{24{1'b0}}, \四位乘法器_7_out_3 };  // Bit_Extender bit_extender_7
  assign bit_extender_8_out = {{24{1'b0}}, \四位乘法器_8_out_3 };  // Bit_Extender bit_extender_8
  Shifter #(.width(32), .shift("ll")) shifter_1 (.in(bit_extender_2_out), .\dist (5'b00100), .out(shifter_1_out));
  Shifter #(.width(32), .shift("ll")) shifter_2 (.in(bit_extender_3_out), .\dist (5'b01000), .out(shifter_2_out));
  Shifter #(.width(32), .shift("ll")) shifter_3 (.in(bit_extender_4_out), .\dist (5'b01100), .out(shifter_3_out));
  Shifter #(.width(32), .shift("ll")) shifter_4 (.in(bit_extender_5_out), .\dist (5'b10000), .out(shifter_4_out));
  Shifter #(.width(32), .shift("ll")) shifter_5 (.in(bit_extender_6_out), .\dist (5'b10100), .out(shifter_5_out));
  Shifter #(.width(32), .shift("ll")) shifter_6 (.in(bit_extender_7_out), .\dist (5'b11000), .out(shifter_6_out));
  Shifter #(.width(32), .shift("ll")) shifter_7 (.in(bit_extender_8_out), .\dist (5'b11100), .out(shifter_7_out));
  Adder #(.width(32)) adder_1 (.a(bit_extender_1_out), .b(shifter_1_out), .out(adder_1_out));  // open: cin, cout
  Adder #(.width(32)) adder_2 (.a(shifter_2_out), .b(shifter_3_out), .out(adder_2_out));  // open: cin, cout
  Adder #(.width(32)) adder_3 (.a(shifter_4_out), .b(shifter_5_out), .out(adder_3_out));  // open: cin, cout
  Adder #(.width(32)) adder_4 (.a(adder_1_out), .b(adder_2_out), .out(adder_4_out));  // open: cin, cout
  Adder #(.width(32)) adder_5 (.a(adder_3_out), .b(shifter_6_out), .out(adder_5_out));  // open: cin, cout
  assign bit_extender_9_out = {{31{1'b0}}, adder_6_cout};  // Bit_Extender bit_extender_9
  assign bit_extender_10_out = {{28{1'b0}}, \四位乘法器_8_out_3 [7:4]};  // Bit_Extender bit_extender_10
  Adder #(.width(32)) adder_6 (.a(adder_4_out), .b(adder_5_out), .out(adder_6_out), .cout(adder_6_cout));  // open: cin
  Adder #(.width(32)) adder_7 (
    .a(bit_extender_9_out), .b(bit_extender_10_out), .out(out_4), .cin(adder_8_cout));  // open: cout
  Adder #(.width(32)) adder_8 (.a(adder_6_out), .b(shifter_7_out), .out(out_3), .cout(adder_8_cout));  // open: cin
endmodule

module \_32X4乘法器测试电路  (
  input  [3:0] in_1,
  input  [31:0] in_2,
  input  [31:0] in_3,
  input  [3:0] in_4,
  output [31:0] out_5,
  output [31:0] out_6,
  output [31:0] out_7,
  output [31:0] out_8
);

  wire [31:0] bit_extender_1_out;

  assign bit_extender_1_out = {{28{1'b0}}, in_4};  // Bit_Extender bit_extender_1
  \_32X4乘法器  \u_32x4乘法器_1  (.in_2(in_2), .in_1(in_1), .out_3(out_5), .out_4(out_6));
  Multiplier #(.width(32)) multiplier_1 (.a(in_3), .b(bit_extender_1_out), .out(out_7), .cout(out_8));  // open: cin
endmodule

module \_32X32乘法器  (
  input  [31:0] in_1,
  input  [31:0] in_2,
  output [31:0] out_3,
  output [31:0] out_4
);

  wire adder_8_cout, adder_13_cout, adder_16_cout, adder_18_cout, adder_19_cout, adder_20_cout, adder_21_cout;
  wire [31:0] adder_1_out, adder_2_out, adder_3_out, adder_4_out, adder_5_out, adder_6_out, adder_7_out,
       adder_8_out, adder_9_out, adder_10_out, adder_11_out, adder_12_out, adder_13_out, adder_14_out,
       adder_15_out, adder_16_out, adder_18_out, adder_19_out, adder_20_out, \n32x4乘法器_1_out_3 ,
       \n32x4乘法器_1_out_4 , \n32x4乘法器_2_out_3 , \n32x4乘法器_2_out_4 , \n32x4乘法器_3_out_3 , \n32x4乘法器_3_out_4 ,
       \n32x4乘法器_4_out_3 , \n32x4乘法器_4_out_4 , \n32x4乘法器_5_out_3 , \n32x4乘法器_5_out_4 , \n32x4乘法器_6_out_3 ,
       \n32x4乘法器_6_out_4 , \n32x4乘法器_7_out_3 , \n32x4乘法器_7_out_4 , \n32x4乘法器_8_out_3 , \n32x4乘法器_8_out_4 ,
       shifter_1_out, shifter_2_out, shifter_3_out, shifter_4_out, shifter_5_out, shifter_6_out,
       shifter_7_out, shifter_8_out, shifter_9_out, shifter_10_out, shifter_11_out, shifter_12_out,
       shifter_13_out, shifter_14_out, shifter_15_out, shifter_16_out, shifter_17_out, shifter_18_out,
       shifter_19_out, shifter_20_out, shifter_21_out;

  \_32X4乘法器  \u_32x4乘法器_1  (.in_2(in_2), .in_1(in_1[3:0]), .out_3(\n32x4乘法器_1_out_3 ), .out_4(\n32x4乘法器_1_out_4 ));
  \_32X4乘法器  \u_32x4乘法器_2  (.in_2(in_2), .in_1(in_1[7:4]), .out_3(\n32x4乘法器_2_out_3 ), .out_4(\n32x4乘法器_2_out_4 ));
  \_32X4乘法器  \u_32x4乘法器_3  (.in_2(in_2), .in_1(in_1[11:8]), .out_3(\n32x4乘法器_3_out_3 ), .out_4(\n32x4乘法器_3_out_4 ));
  \_32X4乘法器  \u_32x4乘法器_4  (.in_2(in_2), .in_1(in_1[15:12]), .out_3(\n32x4乘法器_4_out_3 ), .out_4(\n32x4乘法器_4_out_4 ));
  \_32X4乘法器  \u_32x4乘法器_5  (.in_2(in_2), .in_1(in_1[19:16]), .out_3(\n32x4乘法器_5_out_3 ), .out_4(\n32x4乘法器_5_out_4 ));
  \_32X4乘法器  \u_32x4乘法器_6  (.in_2(in_2), .in_1(in_1[23:20]), .out_3(\n32x4乘法器_6_out_3 ), .out_4(\n32x4乘法器_6_out_4 ));
  \_32X4乘法器  \u_32x4乘法器_7  (.in_2(in_2), .in_1(in_1[27:24]), .out_3(\n32x4乘法器_7_out_3 ), .out_4(\n32x4乘法器_7_out_4 ));
  \_32X4乘法器  \u_32x4乘法器_8  (.in_2(in_2), .in_1(in_1[31:28]), .out_3(\n32x4乘法器_8_out_3 ), .out_4(\n32x4乘法器_8_out_4 ));
  Shifter #(.width(32), .shift("lr")) shifter_1 (.in(\n32x4乘法器_2_out_3 ), .\dist (5'b11100), .out(shifter_1_out));
  Shifter #(.width(32), .shift("lr")) shifter_2 (.in(\n32x4乘法器_3_out_3 ), .\dist (5'b11000), .out(shifter_2_out));
  Shifter #(.width(32), .shift("lr")) shifter_3 (.in(\n32x4乘法器_4_out_3 ), .\dist (5'b10100), .out(shifter_3_out));
  Shifter #(.width(32), .shift("lr")) shifter_4 (.in(\n32x4乘法器_5_out_3 ), .\dist (5'b10000), .out(shifter_4_out));
  Shifter #(.width(32), .shift("lr")) shifter_5 (.in(\n32x4乘法器_6_out_3 ), .\dist (5'b01100), .out(shifter_5_out));
  Shifter #(.width(32), .shift("lr")) shifter_6 (.in(\n32x4乘法器_7_out_3 ), .\dist (5'b01000), .out(shifter_6_out));
  Shifter #(.width(32), .shift("lr")) shifter_7 (.in(\n32x4乘法器_8_out_3 ), .\dist (5'b00100), .out(shifter_7_out));
  Shifter #(.width(32), .shift("ll")) shifter_8 (.in(\n32x4乘法器_2_out_4 ), .\dist (5'b00100), .out(shifter_8_out));
  Shifter #(.width(32), .shift("ll")) shifter_9 (.in(\n32x4乘法器_3_out_4 ), .\dist (5'b01000), .out(shifter_9_out));
  Shifter #(.width(32), .shift("ll")) shifter_10 (.in(\n32x4乘法器_4_out_4 ), .\dist (5'b01100), .out(shifter_10_out));
  Shifter #(.width(32), .shift("ll")) shifter_11 (.in(\n32x4乘法器_5_out_4 ), .\dist (5'b10000), .out(shifter_11_out));
  Shifter #(.width(32), .shift("ll")) shifter_12 (.in(\n32x4乘法器_6_out_4 ), .\dist (5'b10100), .out(shifter_12_out));
  Shifter #(.width(32), .shift("ll")) shifter_13 (.in(\n32x4乘法器_7_out_4 ), .\dist (5'b11000), .out(shifter_13_out));
  Shifter #(.width(32), .shift("ll")) shifter_14 (.in(\n32x4乘法器_8_out_4 ), .\dist (5'b11100), .out(shifter_14_out));
  Adder #(.width(32)) adder_1 (.a(shifter_8_out), .b(shifter_1_out), .out(adder_1_out));  // open: cin, cout
  Adder #(.width(32)) adder_2 (.a(shifter_9_out), .b(shifter_2_out), .out(adder_2_out));  // open: cin, cout
  Adder #(.width(32)) adder_3 (.a(shifter_10_out), .b(shifter_3_out), .out(adder_3_out));  // open: cin, cout
  Shifter #(.width(32), .shift("ll")) shifter_15 (.in(\n32x4乘法器_2_out_3 ), .\dist (5'b00100), .out(shifter_15_out));
  Shifter #(.width(32), .shift("ll")) shifter_16 (.in(\n32x4乘法器_3_out_3 ), .\dist (5'b01000), .out(shifter_16_out));
  Shifter #(.width(32), .shift("ll")) shifter_17 (.in(\n32x4乘法器_4_out_3 ), .\dist (5'b01100), .out(shifter_17_out));
  Shifter #(.width(32), .shift("ll")) shifter_18 (.in(\n32x4乘法器_5_out_3 ), .\dist (5'b10000), .out(shifter_18_out));
  Shifter #(.width(32), .shift("ll")) shifter_19 (.in(\n32x4乘法器_6_out_3 ), .\dist (5'b10100), .out(shifter_19_out));
  Shifter #(.width(32), .shift("ll")) shifter_20 (.in(\n32x4乘法器_7_out_3 ), .\dist (5'b11000), .out(shifter_20_out));
  Shifter #(.width(32), .shift("ll")) shifter_21 (.in(\n32x4乘法器_8_out_3 ), .\dist (5'b11100), .out(shifter_21_out));
  Adder #(.width(32)) adder_4 (.a(shifter_11_out), .b(shifter_4_out), .out(adder_4_out));  // open: cin, cout
  Adder #(.width(32)) adder_5 (.a(shifter_12_out), .b(shifter_5_out), .out(adder_5_out));  // open: cin, cout
  Adder #(.width(32)) adder_6 (.a(shifter_13_out), .b(shifter_6_out), .out(adder_6_out));  // open: cin, cout
  Adder #(.width(32)) adder_7 (
    .a(shifter_14_out), .b(shifter_7_out), .out(adder_7_out), .cin(adder_19_cout));  // open: cout
  Adder #(.width(32)) adder_8 (
    .a(\n32x4乘法器_1_out_3 ), .b(shifter_15_out), .out(adder_8_out), .cout(adder_8_cout));  // open: cin
  Adder #(.width(32)) adder_9 (.a(adder_1_out), .b(adder_2_out), .out(adder_9_out), .cin(adder_13_cout));  // open: cout
  Adder #(.width(32)) adder_10 (.a(adder_3_out), .b(adder_4_out), .out(adder_10_out));  // open: cin, cout
  Adder #(.width(32)) adder_11 (
    .a(adder_5_out), .b(adder_6_out), .out(adder_11_out), .cin(adder_16_cout));  // open: cout
  Adder #(.width(32)) adder_12 (
    .a(adder_9_out), .b(adder_10_out), .out(adder_12_out), .cin(adder_8_cout));  // open: cout
  Adder #(.width(32)) adder_13 (
    .a(adder_8_out), .b(shifter_16_out), .out(adder_13_out), .cout(adder_13_cout));  // open: cin
  Adder #(.width(32)) adder_14 (
    .a(adder_11_out), .b(adder_7_out), .out(adder_14_out), .cin(adder_20_cout));  // open: cout
  Adder #(.width(32)) adder_15 (
    .a(\n32x4乘法器_1_out_4 ), .b(adder_12_out), .out(adder_15_out), .cin(adder_18_cout));  // open: cout
  Adder #(.width(32)) adder_16 (
    .a(adder_13_out), .b(shifter_17_out), .out(adder_16_out), .cout(adder_16_cout));  // open: cin
  Adder #(.width(32)) adder_17 (.a(adder_15_out), .b(adder_14_out), .out(out_4), .cin(adder_21_cout));  // open: cout
  Adder #(.width(32)) adder_18 (
    .a(adder_16_out), .b(shifter_18_out), .out(adder_18_out), .cout(adder_18_cout));  // open: cin
  Adder #(.width(32)) adder_19 (
    .a(adder_18_out), .b(shifter_19_out), .out(adder_19_out), .cout(adder_19_cout));  // open: cin
  Adder #(.width(32)) adder_20 (
    .a(adder_19_out), .b(shifter_20_out), .out(adder_20_out), .cout(adder_20_cout));  // open: cin
  Adder #(.width(32)) adder_21 (.a(adder_20_out), .b(shifter_21_out), .out(out_3), .cout(adder_21_cout));  // open: cin
endmodule

module \_32X32乘法器测试电路  (
  input  [31:0] in_1,
  input  [31:0] in_2,
  input  [31:0] in_3,
  input  [31:0] in_4,
  output [31:0] out_5,
  output [31:0] out_6,
  output [31:0] out_7,
  output [31:0] out_8
);

  Multiplier #(.width(32)) multiplier_1 (.a(in_3), .b(in_4), .out(out_7), .cout(out_8));  // open: cin
  \_32X32乘法器  \u_32x32乘法器_1  (.in_1(in_1), .in_2(in_2), .out_3(out_5), .out_4(out_6));
endmodule
