// Logisim project 实验4-CS1804-U201814604-黄俊淇.circ as structural Verilog: 6 circuits, main circuit 四位除法器
module \四位除法器  (
  input  [3:0] in_1,
  input  [3:0] in_2,
  output [3:0] out_3,
  output [3:0] out_4
);

  wire [7:0] bit_extender_1_out, \四位除法器基本单元_1_out_3 , \四位除法器基本单元_2_out_3 , \四位除法器基本单元_3_out_3 ,
       \四位除法器基本单元_4_out_3 ;

  assign bit_extender_1_out = {{4{1'b0}}, in_1};  // Bit_Extender bit_extender_1
  \四位除法器基本单元  \u_四位除法器基本单元_1  (.in_1(bit_extender_1_out), .in_2(in_2), .out_3(\四位除法器基本单元_1_out_3 ));
  \四位除法器基本单元  \u_四位除法器基本单元_2  (.in_1(\四位除法器基本单元_1_out_3 ), .in_2(in_2), .out_3(\四位除法器基本单元_2_out_3 ));
  \四位除法器基本单元  \u_四位除法器基本单元_3  (.in_1(\四位除法器基本单元_2_out_3 ), .in_2(in_2), .out_3(\四位除法器基本单元_3_out_3 ));
  \四位除法器基本单元  \u_四位除法器基本单元_4  (.in_1(\四位除法器基本单元_3_out_3 ), .in_2(in_2), .out_3(\四位除法器基本单元_4_out_3 ));
  BitSelector #(.width(8), .group(4)) bitselector_1 (.in(\四位除法器基本单元_4_out_3 ), .out(out_3), .sel(1'b0));
  BitSelector #(.width(8), .group(4)) bitselector_2 (.in(\四位除法器基本单元_4_out_3 ), .out(out_4), .sel(1'b1));
endmodule

module \四位除法器测试电路  (
  input  [3:0] in_1,
  input  [3:0] in_2,
  output [3:0] out_3,
  output [3:0] out_4
);

  \四位除法器  \u_四位除法器_1  (.in_1(in_1), .in_2(in_2), .out_3(out_3), .out_4(out_4));
endmodule

module \_32位除法器  (
  input  [31:0] in_1,
  input  [31:0] in_2,
  output [31:0] out_3,
  output [31:0] out_4
);

  wire [31:0] \n32位除法器基本单元_1_out_4 , \n32位除法器基本单元_1_out_5 , \n32位除法器基本单元_2_out_4 , \n32位除法器基本单元_2_out_5 ,
       \n32位除法器基本单元_3_out_4 , \n32位除法器基本单元_3_out_5 , \n32位除法器基本单元_4_out_4 , \n32位除法器基本单元_4_out_5 ,
       \n32位除法器基本单元_5_out_4 , \n32位除法器基本单元_5_out_5 , \n32位除法器基本单元_6_out_4 , \n32位除法器基本单元_6_out_5 ,
       \n32位除法器基本单元_7_out_4 , \n32位除法器基本单元_7_out_5 , \n32位除法器基本单元_8_out_4 , \n32位除法器基本单元_8_out_5 ,
       \n32位除法器基本单元_9_out_4 , \n32位除法器基本单元_9_out_5 , \n32位除法器基本单元_10_out_4 , \n32位除法器基本单元_10_out_5 ,
       \n32位除法器基本单元_11_out_4 , \n32位除法器基本单元_11_out_5 , \n32位除法器基本单元_12_out_4 , \n32位除法器基本单元_12_out_5 ,
       \n32位除法器基本单元_13_out_4 , \n32位除法器基本单元_13_out_5 , \n32位除法器基本单元_14_out_4 , \n32位除法器基本单元_14_out_5 ,
       \n32位除法器基本单元_15_out_4 , \n32位除法器基本单元_15_out_5 , \n32位除法器基本单元_16_out_4 , \n32位除法器基本单元_16_out_5 ,
       \n32位除法器基本单元_17_out_4 , \n32位除法器基本单元_17_out_5 , \n32位除法器基本单元_18_out_4 , \n32位除法器基本单元_18_out_5 ,
       \n32位除法器基本单元_19_out_4 , \n32位除法器基本单元_19_out_5 , \n32位除法器基本单元_20_out_4 , \n32位除法器基本单元_20_out_5 ,
       \n32位除法器基本单元_21_out_4 , \n32位除法器基本单元_21_out_5 , \n32位除法器基本单元_22_out_4 , \n32位除法器基本单元_22_out_5 ,
       \n32位除法器基本单元_23_out_4 , \n32位除法器基本单元_23_out_5 , \n32位除法器基本单元_24_out_4 , \n32位除法器基本单元_24_out_5 ,
       \n32位除法器基本单元_25_out_4 , \n32位除法器基本单元_25_out_5 , \n32位除法器基本单元_26_out_4 , \n32位除法器基本单元_26_out_5 ,
       \n32位除法器基本单元_27_out_4 , \n32位除法器基本单元_27_out_5 , \n32位除法器基本单元_28_out_4 , \n32位除法器基本单元_28_out_5 ,
       \n32位除法器基本单元_29_out_4 , \n32位除法器基本单元_29_out_5 , \n32位除法器基本单元_30_out_4 , \n32位除法器基本单元_30_out_5 ,
       \n32位除法器基本单元_31_out_4 , \n32位除法器基本单元_31_out_5 ;

  // Probe on in_1
  // Probe on in_2
  \_32位除法器基本单元  \u_32位除法器基本单元_1  (
    .in_1(in_1), .in_2({32{1'b0}}), .in_3(in_2), .out_4(\n32位除法器基本单元_1_out_4 ), .out_5(\n32位除法器基本单元_1_out_5 ));
  \_32位除法器基本单元  \u_32位除法器基本单元_2  (
    .in_1(\n32位除法器基本单元_1_out_4 ), .in_2(\n32位除法器基本单元_1_out_5 ), .in_3(in_2), .out_4(\n32位除法器基本单元_2_out_4 ),
    .out_5(\n32位除法器基本单元_2_out_5 ));
  \_32位除法器基本单元  \u_32位除法器基本单元_3  (
    .in_1(\n32位除法器基本单元_2_out_4 ), .in_2(\n32位除法器基本单元_2_out_5 ), .in_3(in_2), .out_4(\n32位除法器基本单元_3_out_4 ),
    .out_5(\n32位除法器基本单元_3_out_5 ));
  \_32位除法器基本单元  \u_32位除法器基本单元_4  (
    .in_1(\n32位除法器基本单元_3_out_4 ), .in_2(\n32位除法器基本单元_3_out_5 ), .in_3(in_2), .out_4(\n32位除法器基本单元_4_out_4 ),
    .out_5(\n32位除法器基本单元_4_out_5 ));
  \_32位除法器基本单元  \u_32位除法器基本单元_5  (
    .in_1(\n32位除法器基本单元_4_out_4 ), .in_2(\n32位除法器基本单元_4_out_5 ), .in_3(in_2), .out_4(\n32位除法器基本单元_5_out_4 ),
    .out_5(\n32位除法器基本单元_5_out_5 ));
  \_32位除法器基本单元  \u_32位除法器基本单元_6  (
    .in_1(\n32位除法器基本单元_5_out_4 ), .in_2(\n32位除法器基本单元_5_out_5 ), .in_3(in_2), .out_4(\n32位除法器基本单元_6_out_4 ),
    .out_5(\n32位除法器基本单元_6_out_5 ));
  \_32位除法器基本单元  \u_32位除法器基本单元_7  (
    .in_1(\n32位除法器基本单元_6_out_4 ), .in_2(\n32位除法器基本单元_6_out_5 ), .in_3(in_2), .out_4(\n32位除法器基本单元_7_out_4 ),
    .out_5(\n32位除法器基本单元_7_out_5 ));
  \_32位除法器基本单元  \u_32位除法器基本单元_8  (
    .in_1(\n32位除法器基本单元_7_out_4 ), .in_2(\n32位除法器基本单元_7_out_5 ), .in_3(in_2), .out_4(\n32位除法器基本单元_8_out_4 ),
    .out_5(\n32位除法器基本单元_8_out_5 ));
  \_32位除法器基本单元  \u_32位除法器基本单元_9  (
    .in_1(\n32位除法器基本单元_8_out_4 ), .in_2(\n32位除法器基本单元_8_out_5 ), .in_3(in_2), .out_4(\n32位除法器基本单元_9_out_4 ),
    .out_5(\n32位除法器基本单元_9_out_5 ));
  \_32位除法器基本单元  \u_32位除法器基本单元_10  (
    .in_1(\n32位除法器基本单元_9_out_4 ), .in_2(\n32位除法器基本单元_9_out_5 ), .in_3(in_2), .out_4(\n32位除法器基本单元_10_out_4 ),
    .out_5(\n32位除法器基本单元_10_out_5 ));
  \_32位除法器基本单元  \u_32位除法器基本单元_11  (
    .in_1(\n32位除法器基本单元_10_out_4 ), .in_2(\n32位除法器基本单元_10_out_5 ), .in_3(in_2),
    .out_4(\n32位除法器基本单元_11_out_4 ), .out_5(\n32位除法器基本单元_11_out_5 ));
  \_32位除法器基本单元  \u_32位除法器基本单元_12  (
    .in_1(\n32位除法器基本单元_11_out_4 ), .in_2(\n32位除法器基本单元_11_out_5 ), .in_3(in_2),
    .out_4(\n32位除法器基本单元_12_out_4 ), .out_5(\n32位除法器基本单元_12_out_5 ));
  \_32位除法器基本单元  \u_32位除法器基本单元_13  (
    .in_1(\n32位除法器基本单元_12_out_4 ), .in_2(\n32位除法器基本单元_12_out_5 ), .in_3(in_2),
    .out_4(\n32位除法器基本单元_13_out_4 ), .out_5(\n32位除法器基本单元_13_out_5 ));
  \_32位除法器基本单元  \u_32位除法器基本单元_14  (
    .in_1(\n32位除法器基本单元_13_out_4 ), .in_2(\n32位除法器基本单元_13_out_5 ), .in_3(in_2),
    .out_4(\n32位除法器基本单元_14_out_4 ), .out_5(\n32位除法器基本单元_14_out_5 ));
  \_32位除法器基本单元  \u_32位除法器基本单元_15  (
    .in_1(\n32位除法器基本单元_14_out_4 ), .in_2(\n32位除法器基本单元_14_out_5 ), .in_3(in_2),
    .out_4(\n32位除法器基本单元_15_out_4 ), .out_5(\n32位除法器基本单元_15_out_5 ));
  \_32位除法器基本单元  \u_32位除法器基本单元_16  (
    .in_1(\n32位除法器基本单元_15_out_4 ), .in_2(\n32位除法器基本单元_15_out_5 ), .in_3(in_2),
    .out_4(\n32位除法器基本单元_16_out_4 ), .out_5(\n32位除法器基本单元_16_out_5 ));
  \_32位除法器基本单元  \u_32位除法器基本单元_17  (
    .in_1(\n32位除法器基本单元_16_out_4 ), .in_2(\n32位除法器基本单元_16_out_5 ), .in_3(in_2),
    .out_4(\n32位除法器基本单元_17_out_4 ), .out_5(\n32位除法器基本单元_17_out_5 ));
  \_32位除法器基本单元  \u_32位除法器基本单元_18  (
    .in_1(\n32位除法器基本单元_17_out_4 ), .in_2(\n32位除法器基本单元_17_out_5 ), .in_3(in_2),
    .out_4(\n32位除法器基本单元_18_out_4 ), .out_5(\n32位除法器基本单元_18_out_5 ));
  \_32位除法器基本单元  \u_32位除法器基本单元_19  (
    .in_1(\n32位除法器基本单元_18_out_4 ), .in_2(\n32位除法器基本单元_18_out_5 ), .in_3(in_2),
    .out_4(\n32位除法器基本单元_19_out_4 ), .out_5(\n32位除法器基本单元_19_out_5 ));
  \_32位除法器基本单元  \u_32位除法器基本单元_20  (
    .in_1(\n32位除法器基本单元_19_out_4 ), .in_2(\n32位除法器基本单元_19_out_5 ), .in_3(in_2),
    .out_4(\n32位除法器基本单元_20_out_4 ), .out_5(\n32位除法器基本单元_20_out_5 ));
  \_32位除法器基本单元  \u_32位除法器基本单元_21  (
    .in_1(\n32位除法器基本单元_20_out_4 ), .in_2(\n32位除法器基本单元_20_out_5 ), .in_3(in_2),
    .out_4(\n32位除法器基本单元_21_out_4 ), .out_5(\n32位除法器基本单元_21_out_5 ));
  \_32位除法器基本单元  \u_32位除法器基本单元_22  (
    .in_1(\n32位除法器基本单元_21_out_4 ), .in_2(\n32位除法器基本单元_21_out_5 ), .in_3(in_2),
    .out_4(\n32位除法器基本单元_22_out_4 ), .out_5(\n32位除法器基本单元_22_out_5 ));
  \_32位除法器基本单元  \u_32位除法器基本单元_23  (
    .in_1(\n32位除法器基本单元_22_out_4 ), .in_2(\n32位除法器基本单元_22_out_5 ), .in_3(in_2),
    .out_4(\n32位除法器基本单元_23_out_4 ), .out_5(\n32位除法器基本单元_23_out_5 ));
  \_32位除法器基本单元  \u_32位除法器基本单元_24  (
    .in_1(\n32位除法器基本单元_23_out_4 ), .in_2(\n32位除法器基本单元_23_out_5 ), .in_3(in_2),
    .out_4(\n32位除法器基本单元_24_out_4 ), .out_5(\n32位除法器基本单元_24_out_5 ));
  \_32位除法器基本单元  \u_32位除法器基本单元_25  (
    .in_1(\n32位除法器基本单元_24_out_4 ), .in_2(\n32位除法器基本单元_24_out_5 ), .in_3(in_2),
    .out_4(\n32位除法器基本单元_25_out_4 ), .out_5(\n32位除法器基本单元_25_out_5 ));
  \_32位除法器基本单元  \u_32位除法器基本单元_26  (
    .in_1(\n32位除法器基本单元_25_out_4 ), .in_2(\n32位除法器基本单元_25_out_5 ), .in_3(in_2),
    .out_4(\n32位除法器基本单元_26_out_4 ), .out_5(\n32位除法器基本单元_26_out_5 ));
  \_32位除法器基本单元  \u_32位除法器基本单元_27  (
    .in_1(\n32位除法器基本单元_26_out_4 ), .in_2(\n32位除法器基本单元_26_out_5 ), .in_3(in_2),
    .out_4(\n32位除法器基本单元_27_out_4 ), .out_5(\n32位除法器基本单元_27_out_5 ));
  \_32位除法器基本单元  \u_32位除法器基本单元_28  (
    .in_1(\n32位除法器基本单元_27_out_4 ), .in_2(\n32位除法器基本单元_27_out_5 ), .in_3(in_2),
    .out_4(\n32位除法器基本单元_28_out_4 ), .out_5(\n32位除法器基本单元_28_out_5 ));
  \_32位除法器基本单元  \u_32位除法器基本单元_29  (
    .in_1(\n32位除法器基本单元_28_out_4 ), .in_2(\n32位除法器基本单元_28_out_5 ), .in_3(in_2),
    .out_4(\n32位除法器基本单元_29_out_4 ), .out_5(\n32位除法器基本单元_29_out_5 ));
  \_32位除法器基本单元  \u_32位除法器基本单元_30  (
    .in_1(\n32位除法器基本单元_29_out_4 ), .in_2(\n32位除法器基本单元_29_out_5 ), .in_3(in_2),
    .out_4(\n32位除法器基本单元_30_out_4 ), .out_5(\n32位除法器基本单元_30_out_5 ));
  \_32位除法器基本单元  \u_32位除法器基本单元_31  (
    .in_1(\n32位除法器基本单元_30_out_4 ), .in_2(\n32位除法器基本单元_30_out_5 ), .in_3(in_2),
    .out_4(\n32位除法器基本单元_31_out_4 ), .out_5(\n32位除法器基本单元_31_out_5 ));
  \_32位除法器基本单元  \u_32位除法器基本单元_32  (
    .in_1(\n32位除法器基本单元_31_out_4 ), .in_2(\n32位除法器基本单元_31_out_5 ), .in_3(in_2), .out_4(out_3), .out_5(out_4));
  // Probe on out_4
  // Probe on out_3
endmodule

module \_32位除法器测试电路  (
  input  [31:0] in_1,
  input  [31:0] in_2,
  output [31:0] out_3,
  output [31:0] out_4
);

  // Probe on in_1
  // Probe on in_2
  \_32位除法器  \u_32位除法器_1  (.in_1(in_1), .in_2(in_2), .out_3(out_3), .out_4(out_4));
  // Probe on out_4
  // Probe on out_3
endmodule

module \四位除法器基本单元  (
  input  [7:0] in_1,
  input  [3:0] in_2,
  output [7:0] out_3
);

  wire comparator_1_lt;
  wire [3:0] bitselector_1_out, bitselector_2_out, multiplexer_1_out, multiplexer_2_out, or_1_out,
       subtractor_1_out;
  wire [7:0] bit_extender_1_out, bit_extender_2_out, shifter_1_out, shifter_2_out;

  Shifter #(.width(8), .shift("ll")) shifter_1 (.in(in_1), .\dist (3'b001), .out(shifter_1_out));
  BitSelector #(.width(8), .group(4)) bitselector_1 (.in(shifter_1_out), .out(bitselector_1_out), .sel(1'b0));
  BitSelector #(.width(8), .group(4)) bitselector_2 (.in(shifter_1_out), .out(bitselector_2_out), .sel(1'b1));
  Comparator #(.width(4), .mode("unsigned")) comparator_1 (
    .a(bitselector_2_out), .b(in_2), .lt(comparator_1_lt));  // open: gt, eq
  Multiplexer #(.select(1), .width(4), .disabled("Z"), .enable("false")) multiplexer_1 (
    .in0(in_2), .in1(4'b0000), .out(multiplexer_1_out), .sel(comparator_1_lt));
  Multiplexer #(.select(1), .width(4), .disabled("Z"), .enable("false")) multiplexer_2 (
    .in0(4'b0001), .in1(4'b0000), .out(multiplexer_2_out), .sel(comparator_1_lt));
  Subtractor #(.width(4)) subtractor_1 (
    .a(bitselector_2_out), .b(multiplexer_1_out), .out(subtractor_1_out));  // open: bin, bout
  assign bit_extender_1_out = {{4{1'b0}}, subtractor_1_out};  // Bit_Extender bit_extender_1
  assign or_1_out = bitselector_1_out | multiplexer_2_out;  // OR_Gate or_1, 4 bits wide
  Shifter #(.width(8), .shift("ll")) shifter_2 (.in(bit_extender_1_out), .\dist (3'b100), .out(shifter_2_out));
  assign bit_extender_2_out = {{4{1'b0}}, or_1_out};  // Bit_Extender bit_extender_2
  assign out_3 = shifter_2_out | bit_extender_2_out;  // OR_Gate or_2, 8 bits wide
endmodule

module \_32位除法器基本单元  (
  input  [31:0] in_1,
  input  [31:0] in_2,
  input  [31:0] in_3,
  output [31:0] out_4,
  output [31:0] out_5
);

  wire bitselector_1_out, comparator_1_lt;
  wire [31:0] bit_extender_1_out, multiplexer_1_out, multiplexer_2_out, or_1_out, shifter_1_out,
       shifter_2_out;

  BitSelector #(.width(32), .group(1)) bitselector_1 (.in(in_1), .out(bitselector_1_out), .sel({5{1'b1}}));
  assign bit_extender_1_out = {{31{1'b0}}, bitselector_1_out};  // Bit_Extender bit_extender_1
  Shifter #(.width(32), .shift("ll")) shifter_1 (.in(in_2), .\dist (5'b00001), .out(shifter_1_out));
  Shifter #(.width(32), .shift("ll")) shifter_2 (.in(in_1), .\dist (5'b00001), .out(shifter_2_out));
  assign or_1_out = bit_extender_1_out | shifter_1_out;  // OR_Gate or_1, 32 bits wide
  Comparator #(.width(32), .mode("unsigned")) comparator_1 (
    .a(or_1_out), .b(in_3), .lt(comparator_1_lt));  // open: gt, eq
  Multiplexer #(.select(1), .width(32), .disabled("Z"), .enable("false")) multiplexer_1 (
    .in0(32'h1), .in1({32{1'b0}}), .out(multiplexer_1_out), .sel(comparator_1_lt));
  Multiplexer #(.select(1), .width(32), .disabled("Z"), .enable("false")) multiplexer_2 (
    .in0(in_3), .in1({32{1'b0}}), .out(multiplexer_2_out), .sel(comparator_1_lt));
  assign out_4 = shifter_2_out | multiplexer_1_out;  // OR_Gate or_2, 32 bits wide
  Subtractor #(.width(32)) subtractor_1 (.a(or_1_out), .b(multiplexer_2_out), .out(out_5));  // open: bin, bout
endmodule
