// Logisim project 实验5-CS1804-U201814604-黄俊淇.circ as structural Verilog
module \四位二进制可逆计数器  (
  input  CPU,
  input  CLR,
  input  LD,
  input  A,
  input  B,
  input  C,
  input  D,
  input  CPD,
  output QA,
  output QB,
  output QC,
  output QD
);

  wire and_1_out, and_2_out, and_3_out, and_4_out, and_5_out, and_6_out, and_7_out, and_8_out, and_9_out,
       and_10_out, and_11_out, and_12_out, and_13_out, and_14_out, c2_out, c3_out, c4_out, not_1_out,
       not_2_out, not_3_out, not_4_out, not_5_out, not_6_out, not_7_out, not_8_out, not_9_out, or_1_out,
       or_2_out, or_3_out, or_4_out, or_5_out;

  or or_1 (or_1_out, CPU, CPD);
  not not_1 (not_1_out, QA);
  not not_2 (not_2_out, QB);
  not not_3 (not_3_out, QC);
  and and_1 (and_1_out, not_1_out, CPD);
  and and_2 (and_2_out, QA, CPU);
  and and_3 (and_3_out, not_1_out, not_2_out, CPD);
  and and_4 (and_4_out, QA, QB, CPU);
  and and_5 (and_5_out, not_1_out, not_2_out, not_3_out, CPD);
  and and_6 (and_6_out, QA, QB, QC, CPU);
  D_Flip_Flop #(.trigger("falling"), .Pre_Clr_Positions("LEGACY"), .NegatePresetClear("false"), .enable("true"), .NewFFLayout("false")) d_ff_1 (
    .clk(or_1_out), .D(not_1_out), .Q(QA), .preset(and_7_out), .reset(or_2_out));  // open: Qn, en
  or c2 (c2_out, and_1_out, and_2_out);
  or c3 (c3_out, and_3_out, and_4_out);
  or c4 (c4_out, and_5_out, and_6_out);
  not not_4 (not_4_out, QD);
  and and_7 (and_7_out, A, not_9_out);
  or or_2 (or_2_out, and_13_out, CLR);
  D_Flip_Flop #(.trigger("falling"), .Pre_Clr_Positions("LEGACY"), .NegatePresetClear("false"), .enable("true"), .NewFFLayout("false")) d_ff_2 (
    .clk(c2_out), .D(not_2_out), .Q(QB), .preset(and_8_out), .reset(or_3_out));  // open: Qn, en
  and and_8 (and_8_out, not_9_out, B);
  or or_3 (or_3_out, CLR, and_14_out);
  D_Flip_Flop #(.trigger("falling"), .Pre_Clr_Positions("LEGACY"), .NegatePresetClear("false"), .enable("true"), .NewFFLayout("false")) d_ff_3 (
    .clk(c3_out), .D(not_3_out), .Q(QC), .preset(and_9_out), .reset(or_4_out));  // open: Qn, en
  and and_9 (and_9_out, not_9_out, C);
  or or_4 (or_4_out, CLR, and_10_out);
  and and_10 (and_10_out, not_9_out, not_7_out);
  D_Flip_Flop #(.trigger("falling"), .Pre_Clr_Positions("LEGACY"), .NegatePresetClear("false"), .enable("true"), .NewFFLayout("false")) d_ff_4 (
    .clk(c4_out), .D(not_4_out), .Q(QD), .preset(and_11_out), .reset(or_5_out));  // open: Qn, en
  and and_11 (and_11_out, not_9_out, D);
  and and_12 (and_12_out, not_9_out, not_8_out);
  or or_5 (or_5_out, and_12_out, CLR);
  and and_13 (and_13_out, not_9_out, not_5_out);
  not not_5 (not_5_out, A);
  and and_14 (and_14_out, not_9_out, not_6_out);
  not not_6 (not_6_out, B);
  not not_7 (not_7_out, C);
  not not_8 (not_8_out, D);
  not not_9 (not_9_out, LD);
endmodule

module \六十进制计数器  (
  input  CLR,
  input  CPu,
  input  CPd,
  input  ADJ,
  output out_5,
  output out_6,
  output out_7,
  output out_8,
  output out_9,
  output out_10,
  output out_11,
  output out_12,
  output out_13
);

  wire and_1_out, and_2_out, and_3_out, and_4_out, and_5_out, and_6_out, and_7_out, and_8_out, clock_1_out,
       nor_1_out, not_1_out, not_2_out, not_3_out, or_1_out, or_2_out, or_3_out, or_4_out;

  and and_1 (and_1_out, CPu, ADJ);
  and and_2 (and_2_out, CPd, ADJ);
  not not_1 (not_1_out, ADJ);
  and and_3 (and_3_out, not_1_out, clock_1_out);
  Clock #(.highDuration(1), .lowDuration(1)) clock_1 (.out(clock_1_out));
  and and_4 (and_4_out, out_9, out_11);
  nor nor_1 (nor_1_out, out_9, out_10, out_11, out_12);
  not not_2 (not_2_out, nor_1_out);
  or or_1 (or_1_out, CLR, and_4_out, out_13);
  or or_2 (or_2_out, and_1_out, and_3_out);
  \四位二进制可逆计数器  \u_四位二进制可逆计数器_1  (
    .CPU(or_2_out), .CPD(and_5_out), .QA(out_12), .A(1'b1), .QB(out_11), .QC(out_10), .QD(out_9), .D(1'b1),
    .CLR(or_1_out), .LD(not_3_out));  // open: B, C
  and and_5 (and_5_out, not_2_out, and_2_out);
  and and_6 (and_6_out, nor_1_out, or_4_out, and_2_out);
  not not_3 (not_3_out, and_6_out);
  and and_7 (and_7_out, out_9, or_2_out, out_12);
  and and_8 (and_8_out, nor_1_out, and_2_out);
  or or_3 (or_3_out, CLR, out_13);
  \四位二进制可逆计数器  \u_四位二进制可逆计数器_2  (
    .CPU(and_7_out), .CPD(and_8_out), .QA(out_8), .QB(out_7), .QC(out_6), .QD(out_5), .CLR(or_3_out),
    .LD(1'b1));  // open: A, B, C, D
  and and_9 (out_13, out_6, out_7);
  or or_4 (or_4_out, out_5, out_6, out_7, out_8);
endmodule

module \六十进制计数器测试电路  (
  input  in_1,
  input  in_2,
  input  in_3,
  input  in_4,
  output out_5
);

  wire d_ff_1_qn, \六十进制计数器_1_out_13 ;
  wire [3:0] \六十进制计数器_1_out_8 , \六十进制计数器_1_out_12 ;

  Hex_Digit_Display hex_digit_display_1 (.value(\六十进制计数器_1_out_8 ));  // open: dp
  Hex_Digit_Display hex_digit_display_2 (.value(\六十进制计数器_1_out_12 ));  // open: dp
  \六十进制计数器  \u_六十进制计数器_1  (
    .CLR(in_4), .CPu(in_1), .CPd(in_3), .ADJ(in_2), .out_9(\六十进制计数器_1_out_12 [3]),
    .out_10(\六十进制计数器_1_out_12 [2]), .out_11(\六十进制计数器_1_out_12 [1]), .out_12(\六十进制计数器_1_out_12 [0]),
    .out_5(\六十进制计数器_1_out_8 [3]), .out_6(\六十进制计数器_1_out_8 [2]), .out_7(\六十进制计数器_1_out_8 [1]),
    .out_8(\六十进制计数器_1_out_8 [0]), .out_13(\六十进制计数器_1_out_13 ));
  D_Flip_Flop #(.trigger("falling"), .Pre_Clr_Positions("ABOVE_BELOW"), .NegatePresetClear("false"), .enable("false"), .NewFFLayout("true")) d_ff_1 (
    .clk(\六十进制计数器_1_out_13 ), .D(d_ff_1_qn), .Q(out_5), .Qn(d_ff_1_qn));  // open: preset, reset
endmodule

module \十二进制计数器或二十四进制的计数器电路  (
  input  in_1,
  input  in_2,
  input  in_3,
  input  in_4,
  input  in_5,
  output out_6,
  output out_7,
  output out_8,
  output out_9,
  output out_10,
  output out_11,
  output out_12,
  output out_13,
  output out_14
);

  wire and_1_out, and_2_out, and_3_out, and_4_out, and_5_out, and_6_out, and_7_out, and_8_out, and_9_out,
       and_10_out, and_11_out, and_12_out, and_13_out, and_14_out, and_15_out, and_16_out, and_17_out,
       and_18_out, and_19_out, and_20_out, and_21_out, and_22_out, not_1_out, not_2_out, not_3_out,
       not_4_out, not_5_out, not_6_out, or_1_out, or_2_out, or_4_out, or_5_out, or_6_out, xor_1_out,
       xor_2_out, xor_3_out, xor_4_out, xor_5_out;
  wire [7:0] adder_1_out, adder_2_out, bit_extender_1_out, \六十进制计数器_1_out_12 , \六十进制计数器_2_out_12 ;

  and and_1 (and_1_out, not_1_out, \六十进制计数器_1_out_12 [4], \六十进制计数器_1_out_12 [1], not_4_out);
  not not_1 (not_1_out, \六十进制计数器_1_out_12 [0]);
  and and_2 (and_2_out, \六十进制计数器_2_out_12 [5], \六十进制计数器_2_out_12 [2], not_2_out, not_3_out);
  not not_2 (not_2_out, \六十进制计数器_2_out_12 [1]);
  \六十进制计数器  \u_六十进制计数器_1  (
    .CLR(or_1_out), .CPu(in_2), .CPd(in_4), .ADJ(in_3), .out_9(\六十进制计数器_1_out_12 [3]),
    .out_10(\六十进制计数器_1_out_12 [2]), .out_11(\六十进制计数器_1_out_12 [1]), .out_12(\六十进制计数器_1_out_12 [0]),
    .out_5(\六十进制计数器_1_out_12 [7]), .out_6(\六十进制计数器_1_out_12 [6]), .out_7(\六十进制计数器_1_out_12 [5]),
    .out_8(\六十进制计数器_1_out_12 [4]));  // open: out_13
  or or_1 (or_1_out, and_1_out, in_5);
  not not_3 (not_3_out, \六十进制计数器_2_out_12 [0]);
  \六十进制计数器  \u_六十进制计数器_2  (
    .CLR(or_2_out), .CPu(in_2), .CPd(in_4), .ADJ(in_3), .out_9(\六十进制计数器_2_out_12 [3]),
    .out_10(\六十进制计数器_2_out_12 [2]), .out_11(\六十进制计数器_2_out_12 [1]), .out_12(\六十进制计数器_2_out_12 [0]),
    .out_5(\六十进制计数器_2_out_12 [7]), .out_6(\六十进制计数器_2_out_12 [6]), .out_7(\六十进制计数器_2_out_12 [5]),
    .out_8(\六十进制计数器_2_out_12 [4]));  // open: out_13
  or or_2 (or_2_out, and_2_out, in_5);
  not not_4 (not_4_out, \六十进制计数器_1_out_12 [3]);
  or or_3 (out_7, and_1_out, and_2_out);
  assign bit_extender_1_out = {{7{1'b0}}, in_1};  // Bit_Extender bit_extender_1
  Adder #(.width(8)) adder_1 (.a(\六十进制计数器_1_out_12 ), .b(8'h1), .out(adder_1_out));  // open: cin, cout
  Adder #(.width(8)) adder_2 (.a(\六十进制计数器_2_out_12 ), .b(bit_extender_1_out), .out(adder_2_out));  // open: cin, cout
  and and_3 (and_3_out, adder_1_out[1], adder_1_out[3]);
  and and_4 (and_4_out, adder_2_out[1], adder_2_out[3]);
  xor xor_1 (xor_1_out, adder_1_out[1], and_3_out);
  xor xor_2 (xor_2_out, and_3_out, adder_1_out[3]);
  or or_4 (or_4_out, and_3_out, adder_1_out[4]);
  xor xor_3 (xor_3_out, adder_2_out[1], and_4_out);
  xor xor_4 (xor_4_out, and_4_out, adder_2_out[3]);
  or or_5 (or_5_out, and_4_out, adder_2_out[4]);
  and and_5 (and_5_out, and_4_out, adder_2_out[4]);
  xor xor_5 (xor_5_out, or_5_out, and_5_out);
  or or_6 (or_6_out, adder_2_out[5], and_5_out);
  and and_6 (and_6_out, adder_2_out[2], or_6_out);
  not not_5 (not_5_out, and_6_out);
  not not_6 (not_6_out, in_1);
  and and_7 (and_7_out, adder_1_out[0], not_6_out);
  and and_8 (and_8_out, xor_1_out, not_6_out);
  and and_9 (and_9_out, not_6_out, adder_1_out[2]);
  and and_10 (and_10_out, xor_2_out, not_6_out);
  and and_11 (and_11_out, or_4_out, not_6_out);
  and and_12 (and_12_out, adder_1_out[5], not_6_out);
  and and_13 (and_13_out, adder_1_out[6], not_6_out);
  and and_14 (and_14_out, adder_1_out[7], not_6_out);
  and and_15 (and_15_out, adder_2_out[0], not_5_out, in_1);
  and and_16 (and_16_out, xor_3_out, not_5_out, in_1);
  and and_17 (and_17_out, in_1, not_5_out, adder_2_out[2]);
  and and_18 (and_18_out, xor_4_out, not_5_out, in_1);
  and and_19 (and_19_out, xor_5_out, not_5_out, in_1);
  and and_20 (and_20_out, or_6_out, not_5_out, in_1);
  and and_21 (and_21_out, adder_2_out[6], in_1);
  and and_22 (and_22_out, adder_2_out[7], in_1);
  or or_7 (out_6, and_7_out, and_15_out);
  or or_8 (out_8, and_8_out, and_16_out);
  or or_9 (out_9, and_9_out, and_17_out);
  or or_10 (out_10, and_10_out, and_18_out);
  or or_11 (out_11, and_11_out, and_19_out);
  or or_12 (out_12, and_12_out, and_20_out);
  or or_13 (out_13, and_13_out, and_21_out);
  or or_14 (out_14, and_14_out, and_22_out);
endmodule

module \十二进制计数器或二十四进制的计数器测试电路  (
  input  in_1,
  input  in_2,
  input  in_3,
  input  in_4,
  input  in_5,
  output out_6
);

  wire d_ff_1_qn, \十二进制计数器或二十四进制的计数器电路_1_out_7 ;
  wire [3:0] \十二进制计数器或二十四进制的计数器电路_1_out_6 , \十二进制计数器或二十四进制的计数器电路_1_out_11 ;

  Hex_Digit_Display hex_digit_display_1 (.value(\十二进制计数器或二十四进制的计数器电路_1_out_11 ));  // open: dp
  Hex_Digit_Display hex_digit_display_2 (.value(\十二进制计数器或二十四进制的计数器电路_1_out_6 ));  // open: dp
  \十二进制计数器或二十四进制的计数器电路  \u_十二进制计数器或二十四进制的计数器电路_1  (
    .in_1(in_3), .in_2(in_1), .in_3(in_2), .in_4(in_4), .in_5(in_5),
    .out_6(\十二进制计数器或二十四进制的计数器电路_1_out_6 [0]), .out_7(\十二进制计数器或二十四进制的计数器电路_1_out_7 ),
    .out_8(\十二进制计数器或二十四进制的计数器电路_1_out_6 [1]), .out_9(\十二进制计数器或二十四进制的计数器电路_1_out_6 [2]),
    .out_10(\十二进制计数器或二十四进制的计数器电路_1_out_6 [3]), .out_11(\十二进制计数器或二十四进制的计数器电路_1_out_11 [0]),
    .out_12(\十二进制计数器或二十四进制的计数器电路_1_out_11 [1]), .out_13(\十二进制计数器或二十四进制的计数器电路_1_out_11 [2]),
    .out_14(\十二进制计数器或二十四进制的计数器电路_1_out_11 [3]));
  D_Flip_Flop #(.trigger("falling"), .Pre_Clr_Positions("ABOVE_BELOW"), .NegatePresetClear("false"), .enable("false"), .NewFFLayout("true")) d_ff_1 (
    .clk(\十二进制计数器或二十四进制的计数器电路_1_out_7 ), .D(d_ff_1_qn), .Q(out_6), .Qn(d_ff_1_qn));  // open: preset, reset
endmodule

module \上下午文字显示的电路  (
  input  AM_FM,
  input  TT,
  output [4:0] out_3,
  output [4:0] out_4,
  output [4:0] out_5,
  output [4:0] out_6
);

  wire [4:0] and_1_out, and_2_out, and_3_out, and_4_out, and_5_out, and_6_out, and_7_out, and_8_out,
       multiplexer_1_out, multiplexer_2_out, not_1_out, not_2_out, not_3_out, not_4_out;

  Multiplexer #(.select(1), .width(5), .disabled("Z"), .enable("false")) multiplexer_1 (
    .in0({5{1'b0}}), .in1({5{1'b1}}), .out(multiplexer_1_out), .sel(AM_FM));
  Multiplexer #(.select(1), .width(5), .disabled("Z"), .enable("false")) multiplexer_2 (
    .in0({5{1'b0}}), .in1({5{1'b1}}), .out(multiplexer_2_out), .sel(TT));
  assign and_1_out = multiplexer_1_out & 5'b10000 & multiplexer_2_out;  // AND_Gate and_1, 5 bits wide
  assign and_2_out = multiplexer_1_out & {5{1'b1}} & multiplexer_2_out;  // AND_Gate and_2, 5 bits wide
  assign and_3_out = multiplexer_1_out & 5'b10100 & multiplexer_2_out;  // AND_Gate and_3, 5 bits wide
  assign and_4_out = multiplexer_1_out & 5'b10000 & multiplexer_2_out;  // AND_Gate and_4, 5 bits wide
  assign not_1_out = ~multiplexer_1_out;  // NOT_Gate not_1, 5 bits wide
  assign not_2_out = ~multiplexer_1_out;  // NOT_Gate not_2, 5 bits wide
  assign not_3_out = ~multiplexer_1_out;  // NOT_Gate not_3, 5 bits wide
  assign not_4_out = ~multiplexer_1_out;  // NOT_Gate not_4, 5 bits wide
  assign and_5_out = 5'b00001 & not_1_out & multiplexer_2_out;  // AND_Gate and_5, 5 bits wide
  assign and_6_out = {5{1'b1}} & not_2_out & multiplexer_2_out;  // AND_Gate and_6, 5 bits wide
  assign and_7_out = 5'b00101 & not_3_out & multiplexer_2_out;  // AND_Gate and_7, 5 bits wide
  assign and_8_out = 5'b00001 & not_4_out & multiplexer_2_out;  // AND_Gate and_8, 5 bits wide
  assign out_3 = and_5_out | and_1_out;  // OR_Gate or_1, 5 bits wide
  assign out_4 = and_6_out | and_2_out;  // OR_Gate or_2, 5 bits wide
  assign out_5 = and_7_out | and_3_out;  // OR_Gate or_3, 5 bits wide
  assign out_6 = and_8_out | and_4_out;  // OR_Gate or_4, 5 bits wide
endmodule

module \上下午文字显示测试电路  (
  input  AM_FM,
  input  TT
);

  wire [4:0] \上下午文字显示的电路_1_out_3 , \上下午文字显示的电路_1_out_4 , \上下午文字显示的电路_1_out_5 , \上下午文字显示的电路_1_out_6 ;

  DotMatrix #(.inputtype("column"), .matrixcols(4), .matrixrows(5), .persist(0), .dotshape("square")) dotmatrix_1 (
    .col0(\上下午文字显示的电路_1_out_3 ), .col1(\上下午文字显示的电路_1_out_4 ), .col2(\上下午文字显示的电路_1_out_5 ),
    .col3(\上下午文字显示的电路_1_out_6 ));
  \上下午文字显示的电路  \u_上下午文字显示的电路_1  (
    .AM_FM(AM_FM), .TT(TT), .out_3(\上下午文字显示的电路_1_out_3 ), .out_4(\上下午文字显示的电路_1_out_4 ),
    .out_5(\上下午文字显示的电路_1_out_5 ), .out_6(\上下午文字显示的电路_1_out_6 ));
endmodule

module \电子钟整点报时电路  (
  input  in_1,
  input  in_2,
  input  in_3,
  input  in_4,
  input  in_5,
  input  in_6,
  input  in_7,
  input  in_8,
  input  in_9,
  input  in_10,
  input  in_11,
  input  in_12,
  input  in_13,
  output out_14
);

  wire and_1_out, and_3_out, and_4_out, not_1_out, not_2_out, not_3_out, not_4_out, not_5_out, not_6_out;

  and and_1 (and_1_out, not_1_out, in_2, not_2_out, in_4);
  not not_1 (not_1_out, in_1);
  not not_2 (not_2_out, in_3);
  and and_2 (out_14, and_1_out, and_3_out, and_4_out, in_13);
  and and_3 (and_3_out, in_5, not_4_out, not_3_out, in_8);
  not not_3 (not_3_out, in_7);
  not not_4 (not_4_out, in_6);
  not not_5 (not_5_out, in_9);
  and and_4 (and_4_out, not_5_out, in_10, not_6_out, in_12);
  not not_6 (not_6_out, in_11);
endmodule

module \电子钟整点报时电路测试电路  (
  input  in_1,
  input  in_2,
  input  in_3,
  input  in_4,
  input  in_5,
  input  in_6,
  input  in_7,
  input  in_8,
  input  in_9,
  input  in_10,
  input  in_11,
  input  in_12,
  input  in_13,
  output out_14
);

  \电子钟整点报时电路  \u_电子钟整点报时电路_1  (
    .out_14(out_14), .in_1(in_1), .in_2(in_2), .in_3(in_3), .in_4(in_4), .in_5(in_5), .in_6(in_6),
    .in_7(in_7), .in_8(in_8), .in_9(in_9), .in_10(in_10), .in_11(in_11), .in_12(in_12), .in_13(in_13));
endmodule

module \秒脉冲产生电路  (
  input  in_1,
  output out_2
);

  wire d_ff_1_q, d_ff_1_qn, d_ff_2_qn;

  D_Flip_Flop #(.trigger("falling"), .Pre_Clr_Positions("ABOVE_BELOW"), .NegatePresetClear("false"), .enable("false"), .NewFFLayout("true")) d_ff_1 (
    .clk(in_1), .D(d_ff_1_qn), .Q(d_ff_1_q), .Qn(d_ff_1_qn));  // open: preset, reset
  D_Flip_Flop #(.trigger("falling"), .Pre_Clr_Positions("ABOVE_BELOW"), .NegatePresetClear("false"), .enable("false"), .NewFFLayout("true")) d_ff_2 (
    .clk(d_ff_1_q), .D(d_ff_2_qn), .Q(out_2), .Qn(d_ff_2_qn));  // open: preset, reset
endmodule

module \多功能数字钟  (
  input  CPu,
  input  CP,
  input  in_3,
  input  CPd,
  input  CLR,
  input  Adj0,
  input  in_7,
  output [3:0] out_8,
  output [3:0] out_9,
  output [3:0] out_10,
  output [3:0] out_11,
  output [4:0] out_12,
  output [4:0] out_13,
  output [4:0] out_14,
  output [4:0] out_15,
  output out_16,
  output [3:0] out_17,
  output [3:0] out_18
);

  wire and_1_out, and_2_out, and_3_out, and_4_out, and_5_out, and_6_out, not_1_out, not_2_out, not_3_out,
       not_4_out, or_1_out, or_2_out, or_3_out, or_4_out, t_ff_1_q, \六十进制计数器_1_out_13 , \六十进制计数器_2_out_13 ,
       \十二进制计数器或二十四进制的计数器电路_1_out_7 , \秒脉冲产生电路_1_out_2 ;

  \秒脉冲产生电路  \u_秒脉冲产生电路_1  (.in_1(CP), .out_2(\秒脉冲产生电路_1_out_2 ));
  not not_1 (not_1_out, Adj0);
  and and_1 (and_1_out, Adj0, in_7);
  not not_2 (not_2_out, Adj0);
  not not_3 (not_3_out, in_7);
  \六十进制计数器  \u_六十进制计数器_1  (
    .CLR(CLR), .CPu(\秒脉冲产生电路_1_out_2 ), .CPd(1'b0), .ADJ(1'b1), .out_9(out_9[3]), .out_10(out_9[2]),
    .out_11(out_9[1]), .out_12(out_9[0]), .out_5(out_8[3]), .out_6(out_8[2]), .out_7(out_8[1]),
    .out_8(out_8[0]), .out_13(\六十进制计数器_1_out_13 ));
  and and_2 (and_2_out, CPu, and_1_out);
  or or_1 (or_1_out, not_1_out, Adj0);
  and and_3 (and_3_out, and_1_out, CPd);
  or or_2 (or_2_out, and_2_out, \六十进制计数器_1_out_13 );
  and and_4 (and_4_out, Adj0, not_3_out);
  \六十进制计数器  \u_六十进制计数器_2  (
    .CLR(CLR), .CPu(or_2_out), .CPd(and_3_out), .ADJ(or_1_out), .out_9(out_11[3]), .out_10(out_11[2]),
    .out_11(out_11[1]), .out_12(out_11[0]), .out_5(out_10[3]), .out_6(out_10[2]), .out_7(out_10[1]),
    .out_8(out_10[0]), .out_13(\六十进制计数器_2_out_13 ));
  \电子钟整点报时电路  \u_电子钟整点报时电路_1  (
    .out_14(out_16), .in_1(out_10[3]), .in_2(out_10[2]), .in_3(out_10[1]), .in_4(out_10[0]),
    .in_5(out_11[3]), .in_6(out_11[2]), .in_7(out_11[1]), .in_8(out_11[0]), .in_9(out_8[3]),
    .in_10(out_8[2]), .in_11(out_8[1]), .in_12(out_8[0]), .in_13(CP));
  and and_5 (and_5_out, CPu, and_4_out);
  or or_3 (or_3_out, and_5_out, \六十进制计数器_2_out_13 );
  or or_4 (or_4_out, not_2_out, Adj0);
  and and_6 (and_6_out, and_4_out, CPd);
  \十二进制计数器或二十四进制的计数器电路  \u_十二进制计数器或二十四进制的计数器电路_1  (
    .in_1(in_3), .in_2(or_3_out), .in_3(or_4_out), .in_4(and_6_out), .in_5(CLR), .out_6(out_18[0]),
    .out_7(\十二进制计数器或二十四进制的计数器电路_1_out_7 ), .out_8(out_18[1]), .out_9(out_18[2]), .out_10(out_18[3]),
    .out_11(out_17[0]), .out_12(out_17[1]), .out_13(out_17[2]), .out_14(out_17[3]));
  T_Flip_Flop #(.trigger("rising"), .Pre_Clr_Positions("ABOVE_BELOW"), .NegatePresetClear("false"), .enable("false"), .NewFFLayout("true")) t_ff_1 (
    .clk(\十二进制计数器或二十四进制的计数器电路_1_out_7 ), .T(1'b1), .Q(t_ff_1_q), .reset(CLR));  // open: Qn, preset
  \上下午文字显示的电路  \u_上下午文字显示的电路_1  (
    .AM_FM(t_ff_1_q), .TT(not_4_out), .out_3(out_15), .out_4(out_14), .out_5(out_13), .out_6(out_12));
  not not_4 (not_4_out, in_3);
endmodule

module \多功能数字钟测试电路  (
  input  in_1,
  input  in_2,
  input  in_3,
  input  in_4
);

  wire button_1_out, button_2_out, clock_1_out, \多功能数字钟_1_out_16 ;
  wire [3:0] \多功能数字钟_1_out_8 , \多功能数字钟_1_out_9 , \多功能数字钟_1_out_10 , \多功能数字钟_1_out_11 , \多功能数字钟_1_out_17 ,
       \多功能数字钟_1_out_18 ;
  wire [4:0] \多功能数字钟_1_out_12 , \多功能数字钟_1_out_13 , \多功能数字钟_1_out_14 , \多功能数字钟_1_out_15 ;

  DotMatrix #(.inputtype("column"), .matrixcols(4), .matrixrows(5), .persist(0), .dotshape("square")) dotmatrix_1 (
    .col0(\多功能数字钟_1_out_15 ), .col1(\多功能数字钟_1_out_14 ), .col2(\多功能数字钟_1_out_13 ), .col3(\多功能数字钟_1_out_12 ));
  Hex_Digit_Display hex_digit_display_1 (.value(\多功能数字钟_1_out_17 ));  // open: dp
  \多功能数字钟  \u_多功能数字钟_1  (
    .out_8(\多功能数字钟_1_out_8 ), .out_9(\多功能数字钟_1_out_9 ), .out_10(\多功能数字钟_1_out_10 ),
    .out_11(\多功能数字钟_1_out_11 ), .out_17(\多功能数字钟_1_out_17 ), .out_18(\多功能数字钟_1_out_18 ), .CPu(button_1_out),
    .CP(clock_1_out), .CPd(button_2_out), .CLR(in_4), .Adj0(in_1), .in_7(in_2), .out_12(\多功能数字钟_1_out_12 ),
    .out_13(\多功能数字钟_1_out_13 ), .out_14(\多功能数字钟_1_out_14 ), .out_15(\多功能数字钟_1_out_15 ),
    .out_16(\多功能数字钟_1_out_16 ), .in_3(in_3));
  Clock #(.highDuration(1), .lowDuration(1)) clock_1 (.out(clock_1_out));
  Hex_Digit_Display hex_digit_display_2 (.value(\多功能数字钟_1_out_18 ));  // open: dp
  Hex_Digit_Display hex_digit_display_3 (.value(\多功能数字钟_1_out_10 ));  // open: dp
  Button button_1 (.out(button_1_out));
  Button button_2 (.out(button_2_out));
  Hex_Digit_Display hex_digit_display_4 (.value(\多功能数字钟_1_out_8 ));  // open: dp
  Hex_Digit_Display hex_digit_display_5 (.value(\多功能数字钟_1_out_11 ));  // open: dp
  Hex_Digit_Display hex_digit_display_6 (.value(\多功能数字钟_1_out_9 ));  // open: dp
  LED #(.active("true")) led_1 (.in(\多功能数字钟_1_out_16 ));
endmodule

module _12_24 (
  input  in_1,
  input  in_2,
  input  in_3,
  input  in_4,
  input  in_5,
  output out_6,
  output out_7,
  output out_8,
  output out_9,
  output out_10,
  output out_11,
  output out_12,
  output out_13,
  output out_14
);

  wire and_1_out, and_2_out, and_3_out, and_4_out, and_5_out, not_1_out, not_2_out, not_3_out, not_4_out,
       not_5_out, not_6_out, or_2_out;
  wire [4:1] adder_1_out;
  wire [7:0] bit_extender_1_out, \六十进制计数器_1_out_12 ;

  not not_1 (not_1_out, in_1);
  and and_1 (and_1_out, in_1, and_2_out);
  and and_2 (and_2_out, \六十进制计数器_1_out_12 [5], \六十进制计数器_1_out_12 [2], not_5_out, not_6_out);
  or or_1 (out_6, and_1_out, and_3_out);
  not not_2 (not_2_out, in_1);
  and and_3 (and_3_out, not_2_out, and_4_out);
  and and_4 (and_4_out, not_3_out, \六十进制计数器_1_out_12 [4], \六十进制计数器_1_out_12 [1], not_4_out);
  not not_3 (not_3_out, \六十进制计数器_1_out_12 [0]);
  \六十进制计数器  \u_六十进制计数器_1  (
    .CLR(or_2_out), .CPu(in_2), .CPd(in_4), .ADJ(in_3), .out_9(\六十进制计数器_1_out_12 [3]),
    .out_10(\六十进制计数器_1_out_12 [2]), .out_11(\六十进制计数器_1_out_12 [1]), .out_12(\六十进制计数器_1_out_12 [0]),
    .out_5(\六十进制计数器_1_out_12 [7]), .out_6(\六十进制计数器_1_out_12 [6]), .out_7(\六十进制计数器_1_out_12 [5]),
    .out_8(\六十进制计数器_1_out_12 [4]));  // open: out_13
  not not_4 (not_4_out, \六十进制计数器_1_out_12 [3]);
  not not_5 (not_5_out, \六十进制计数器_1_out_12 [0]);
  or or_2 (or_2_out, out_6, in_5);
  not not_6 (not_6_out, \六十进制计数器_1_out_12 [1]);
  assign bit_extender_1_out = {{7{1'b0}}, not_1_out};  // Bit_Extender bit_extender_1
  Adder #(.width(8)) adder_1 (
    .a(\六十进制计数器_1_out_12 ), .b(bit_extender_1_out),
    .out({out_14, out_13, out_12, adder_1_out[4:3], out_9, adder_1_out[1], out_7}));  // open: cin, cout
  and and_5 (and_5_out, adder_1_out[1], adder_1_out[3]);
  xor xor_1 (out_8, adder_1_out[1], and_5_out);
  xor xor_2 (out_10, and_5_out, adder_1_out[3]);
  or or_3 (out_11, and_5_out, adder_1_out[4]);
endmodule
